// Logisim project 四位二进制可逆计数器.circ as structural Verilog: 2 circuits, main circuit main
module main (
  input  \置零 ,
  input  CPU,
  input  CPD,
  output Q3,
  output Q2,
  output Q1,
  output Q0
);

  wire and_1_out, and_2_out, and_3_out, and_4_out, and_5_out, and_6_out, D0_qn, D1_qn, D2_qn, D3_qn,
       or_1_out, or_2_out, or_3_out, or_4_out;

  or or_1 (or_1_out, and_1_out, and_2_out);
  and and_1 (and_1_out, CPD, D2_qn, D1_qn, D0_qn);
  and and_2 (and_2_out, CPU, Q0, Q1, Q2);
  D_Flip_Flop #(.trigger("falling")) D3 (
    .clk(or_1_out), .D(D3_qn), .Q(Q3), .Qn(D3_qn), .reset(\置零 ));  // open: preset, en
  or or_2 (or_2_out, and_4_out, and_3_out);
  and and_3 (and_3_out, CPU, Q0, Q1);
  and and_4 (and_4_out, CPD, D1_qn, D0_qn);
  D_Flip_Flop #(.trigger("falling")) D2 (
    .clk(or_2_out), .D(D2_qn), .Q(Q2), .Qn(D2_qn), .reset(\置零 ));  // open: preset, en
  or or_3 (or_3_out, and_5_out, and_6_out);
  and and_5 (and_5_out, CPD, D0_qn);
  and and_6 (and_6_out, CPU, Q0);
  D_Flip_Flop #(.trigger("falling")) D1 (
    .clk(or_3_out), .D(D1_qn), .Q(Q1), .Qn(D1_qn), .reset(\置零 ));  // open: preset, en
  or or_4 (or_4_out, CPD, CPU);
  D_Flip_Flop #(.trigger("falling")) D0 (
    .clk(or_4_out), .D(D0_qn), .Q(Q0), .Qn(D0_qn), .reset(\置零 ));  // open: preset, en
endmodule

module \四位二进制可逆计数器封装版  (
  input  in_1,
  input  in_2,
  input  in_3,
  output out_4,
  output out_5,
  output out_6,
  output out_7
);

  main main_1 (.\置零 (in_2), .CPU(in_1), .CPD(in_3), .Q3(out_4), .Q2(out_5), .Q1(out_6), .Q0(out_7));
endmodule
