// Logisim project 一位二进制全加器.circ as structural Verilog: 1 circuit, main circuit main
module main (
  input  A,
  input  B,
  input  Ci,
  output S,
  output Co
);

  wire nand_1_out, nand_2_out, xor_1_out;

  xor xor_1 (xor_1_out, A, B);
  nand nand_1 (nand_1_out, xor_1_out, Ci);
  nand nand_2 (nand_2_out, B, A);
  xor xor_2 (S, xor_1_out, Ci);
  nand nand_3 (Co, nand_1_out, nand_2_out);
endmodule
