// Logisim project 串行进位的四位二进制并行加法器.circ as structural Verilog: 1 circuit, main circuit main
module main (
  input  C0,
  input  A3,
  input  B3,
  input  A0,
  input  B0,
  input  A1,
  input  B1,
  input  A2,
  input  B2,
  output S0,
  output S1,
  output S2,
  output S3,
  output C4
);

  wire nand_1_out, nand_2_out, nand_3_out, nand_4_out, nand_5_out, nand_6_out, nand_7_out, nand_8_out,
       nand_9_out, nand_10_out, nand_11_out, xor_2_out, xor_4_out, xor_6_out, xor_8_out;

  xor xor_1 (S0, C0, xor_2_out);
  xor xor_2 (xor_2_out, A0, B0);
  nand nand_1 (nand_1_out, xor_2_out, C0);
  nand nand_2 (nand_2_out, A0, B0);
  nand nand_3 (nand_3_out, nand_1_out, nand_2_out);
  xor xor_3 (S1, nand_3_out, xor_4_out);
  xor xor_4 (xor_4_out, A1, B1);
  nand nand_4 (nand_4_out, xor_4_out, nand_3_out);
  nand nand_5 (nand_5_out, A1, B1);
  xor xor_5 (S2, nand_6_out, xor_6_out);
  nand nand_6 (nand_6_out, nand_4_out, nand_5_out);
  xor xor_6 (xor_6_out, A2, B2);
  nand nand_7 (nand_7_out, xor_6_out, nand_6_out);
  nand nand_8 (nand_8_out, nand_7_out, nand_9_out);
  nand nand_9 (nand_9_out, A2, B2);
  xor xor_7 (S3, nand_8_out, xor_8_out);
  xor xor_8 (xor_8_out, A3, B3);
  nand nand_10 (nand_10_out, xor_8_out, nand_8_out);
  nand nand_11 (nand_11_out, A3, B3);
  nand nand_12 (C4, nand_10_out, nand_11_out);
endmodule
