// Logisim project 先行进位的四位二进制并行加法器.circ as structural Verilog: 6 circuits, main circuit 先行进位的四位二进制并行加法器
module \先行进位的四位二进制并行加法器  (
  input  C0,
  input  A0,
  input  B0,
  input  A1,
  input  B1,
  input  A2,
  input  B2,
  input  A3,
  input  B3,
  output S0,
  output S1,
  output S2,
  output S3,
  output C4
);

  wire and_1_out, and_2_out, and_3_out, and_4_out, and_5_out, and_6_out, and_7_out, and_8_out, and_9_out,
       and_10_out, C1_out, C2_out, C3_out, G1_out, G2_out, G3_out, G4_out, P1_out, P2_out, P3_out, P4_out;

  xor P1 (P1_out, A0, B0);
  xor P2 (P2_out, A1, B1);
  xor P3 (P3_out, A2, B2);
  xor P4 (P4_out, A3, B3);
  and G1 (G1_out, A0, B0);
  and G2 (G2_out, A1, B1);
  and G3 (G3_out, A2, B2);
  and G4 (G4_out, A3, B3);
  and and_1 (and_1_out, C0, P1_out);
  and and_2 (and_2_out, C0, P1_out, P2_out);
  and and_3 (and_3_out, P2_out, G1_out);
  and and_4 (and_4_out, C0, P1_out, P2_out, P3_out);
  and and_5 (and_5_out, P2_out, P3_out, G1_out);
  and and_6 (and_6_out, P3_out, G2_out);
  and and_7 (and_7_out, C0, P1_out, P2_out, P3_out, P4_out);
  and and_8 (and_8_out, P2_out, P3_out, P4_out, G1_out);
  and and_9 (and_9_out, P3_out, P4_out, G2_out);
  and and_10 (and_10_out, P4_out, G3_out);
  or C1 (C1_out, and_1_out, G1_out);
  or C2 (C2_out, and_2_out, G2_out, and_3_out);
  or C3 (C3_out, and_4_out, and_5_out, and_6_out, G3_out);
  xor u_S0 (S0, C0, P1_out);
  xor u_S1 (S1, C1_out, P2_out);
  xor u_S2 (S2, C2_out, P3_out);
  xor u_S3 (S3, C3_out, P4_out);
  or u_C4 (C4, and_7_out, and_8_out, G4_out, and_9_out, and_10_out);
endmodule

module \并行加法器封装版  (
  input  C0,
  input  A3,
  input  A2,
  input  A1,
  input  A0,
  input  B3,
  input  B2,
  input  B1,
  input  B0,
  output S3,
  output S2,
  output S1,
  output S0,
  output C4
);

  \先行进位的四位二进制并行加法器  \u_先行进位的四位二进制并行加法器_1  (
    .A0(A0), .B0(B0), .A1(A1), .B1(B1), .A2(A2), .B2(B2), .A3(A3), .B3(B3), .S0(S0), .S1(S1), .S2(S2),
    .S3(S3), .C4(C4), .C0(C0));
endmodule

module \二进制转8421BCD码电路  (
  input  in_1,
  input  in_2,
  input  in_3,
  input  in_4,
  output S80,
  output S40,
  output S20,
  output S10,
  output S8,
  output S4,
  output S2,
  output S1
);

  wire and_1_out, or_1_out;

  \先行进位的四位二进制并行加法器  \u_先行进位的四位二进制并行加法器_1  (
    .A0(in_4), .B0(1'b0), .A1(in_3), .B1(and_1_out), .A2(in_2), .B2(and_1_out), .A3(in_1), .B3(1'b0),
    .S0(S1), .S1(S2), .S2(S4), .S3(S8), .C4(S10), .C0(1'b0));
  and and_1 (and_1_out, in_1, or_1_out);
  or or_1 (or_1_out, in_3, in_2);

  assign S20 = 1'b0;
  assign S40 = 1'b0;
  assign S80 = 1'b0;
endmodule

module \二进制数转8421码电路封装版  (
  input  in_1,
  input  in_2,
  input  in_3,
  input  in_4,
  output S40,
  output S10,
  output S4,
  output S1,
  output S80,
  output S20,
  output S8,
  output S2
);

  \二进制转8421BCD码电路  \u_二进制转8421bcd码电路_1  (
    .S80(S80), .S40(S40), .S20(S20), .S10(S10), .S8(S8), .S4(S4), .S2(S2), .S1(S1), .in_1(in_1), .in_2(in_2),
    .in_3(in_3), .in_4(in_4));
endmodule

module \_7段译码器译码电路  (
  input  A3,
  input  A2,
  input  A1,
  input  A0,
  output a,
  output b,
  output c,
  output d,
  output e,
  output f,
  output g
);

  wire and_1_out, and_2_out, and_3_out, and_4_out, and_5_out, and_6_out, and_7_out, and_8_out, and_9_out,
       and_10_out, and_11_out, and_12_out, and_13_out, and_14_out, and_15_out, and_16_out, and_17_out,
       and_18_out, and_19_out, and_20_out, and_21_out, and_22_out, and_23_out, and_24_out, and_25_out,
       not_1_out, not_2_out, not_3_out, not_4_out;

  not not_1 (not_1_out, A3);
  not not_2 (not_2_out, A2);
  not not_3 (not_3_out, A1);
  not not_4 (not_4_out, A0);
  and and_1 (and_1_out, not_2_out, not_3_out, not_4_out);
  and and_2 (and_2_out, not_1_out, not_2_out, A1);
  and and_3 (and_3_out, not_1_out, A2, A0);
  and and_4 (and_4_out, A3, not_3_out, A0);
  and and_5 (and_5_out, not_1_out, not_2_out);
  and and_6 (and_6_out, not_3_out, not_4_out);
  and and_7 (and_7_out, not_2_out, not_3_out);
  and and_8 (and_8_out, not_1_out, A1, A0);
  and and_9 (and_9_out, not_1_out, A2);
  and and_10 (and_10_out, not_3_out, not_4_out);
  and and_11 (and_11_out, not_2_out, A0);
  and and_12 (and_12_out, A2, not_3_out, A0);
  and and_13 (and_13_out, not_2_out, not_4_out);
  and and_14 (and_14_out, not_2_out, A1, A0);
  and and_15 (and_15_out, A2, A1, not_4_out);
  and and_16 (and_16_out, A1, not_4_out);
  and and_17 (and_17_out, not_2_out, not_4_out);
  and and_18 (and_18_out, not_3_out, not_4_out);
  and and_19 (and_19_out, A2, not_3_out);
  and and_20 (and_20_out, A3, not_2_out, not_3_out);
  and and_21 (and_21_out, A2, not_4_out);
  and and_22 (and_22_out, A2, not_3_out);
  and and_23 (and_23_out, A3, not_2_out);
  and and_24 (and_24_out, not_2_out, A1);
  and and_25 (and_25_out, A1, not_4_out);
  or or_1 (a, and_1_out, and_2_out, and_3_out, and_4_out);
  or or_2 (b, and_5_out, and_6_out, and_7_out, and_8_out);
  or or_3 (c, and_9_out, and_10_out, and_11_out);
  or or_4 (d, and_12_out, and_13_out, and_14_out, and_15_out);
  or or_5 (e, and_16_out, and_17_out);
  or or_6 (f, and_18_out, and_19_out, and_20_out, and_21_out);
  or or_7 (g, and_22_out, and_23_out, and_24_out, and_25_out);
endmodule

module \显示电路  (
  input  in_1,
  input  in_2,
  input  in_3,
  input  in_4
);

  wire \n7段译码器译码电路_1_a , \n7段译码器译码电路_1_b , \n7段译码器译码电路_1_c , \n7段译码器译码电路_1_d , \n7段译码器译码电路_1_e ,
       \n7段译码器译码电路_1_f , \n7段译码器译码电路_1_g , \n7段译码器译码电路_2_a , \n7段译码器译码电路_2_b , \n7段译码器译码电路_2_c ,
       \n7段译码器译码电路_2_d , \n7段译码器译码电路_2_e , \n7段译码器译码电路_2_f , \n7段译码器译码电路_2_g , \二进制数转8421码电路封装版_1_s1 ,
       \二进制数转8421码电路封装版_1_s2 , \二进制数转8421码电路封装版_1_s4 , \二进制数转8421码电路封装版_1_s8 , \二进制数转8421码电路封装版_1_s10 ,
       \二进制数转8421码电路封装版_1_s20 , \二进制数转8421码电路封装版_1_s40 , \二进制数转8421码电路封装版_1_s80 ;

  \_7段译码器译码电路  \u_7段译码器译码电路_1  (
    .A3(\二进制数转8421码电路封装版_1_s80 ), .A2(\二进制数转8421码电路封装版_1_s40 ), .A1(\二进制数转8421码电路封装版_1_s20 ),
    .A0(\二进制数转8421码电路封装版_1_s10 ), .a(\n7段译码器译码电路_1_a ), .b(\n7段译码器译码电路_1_b ), .c(\n7段译码器译码电路_1_c ),
    .d(\n7段译码器译码电路_1_d ), .e(\n7段译码器译码电路_1_e ), .f(\n7段译码器译码电路_1_f ), .g(\n7段译码器译码电路_1_g ));
  _7_Segment_Display u_7_segment_display_1 (
    .g(\n7段译码器译码电路_1_g ), .f(\n7段译码器译码电路_1_f ), .a(\n7段译码器译码电路_1_a ), .b(\n7段译码器译码电路_1_b ),
    .e(\n7段译码器译码电路_1_e ), .d(\n7段译码器译码电路_1_d ), .c(\n7段译码器译码电路_1_c ));  // open: dp
  \二进制数转8421码电路封装版  \u_二进制数转8421码电路封装版_1  (
    .S80(\二进制数转8421码电路封装版_1_s80 ), .S40(\二进制数转8421码电路封装版_1_s40 ), .S20(\二进制数转8421码电路封装版_1_s20 ),
    .S10(\二进制数转8421码电路封装版_1_s10 ), .S8(\二进制数转8421码电路封装版_1_s8 ), .S4(\二进制数转8421码电路封装版_1_s4 ),
    .S2(\二进制数转8421码电路封装版_1_s2 ), .S1(\二进制数转8421码电路封装版_1_s1 ), .in_1(in_1), .in_2(in_2), .in_3(in_3),
    .in_4(in_4));
  \_7段译码器译码电路  \u_7段译码器译码电路_2  (
    .A3(\二进制数转8421码电路封装版_1_s8 ), .A2(\二进制数转8421码电路封装版_1_s4 ), .A1(\二进制数转8421码电路封装版_1_s2 ),
    .A0(\二进制数转8421码电路封装版_1_s1 ), .a(\n7段译码器译码电路_2_a ), .b(\n7段译码器译码电路_2_b ), .c(\n7段译码器译码电路_2_c ),
    .d(\n7段译码器译码电路_2_d ), .e(\n7段译码器译码电路_2_e ), .f(\n7段译码器译码电路_2_f ), .g(\n7段译码器译码电路_2_g ));
  _7_Segment_Display u_7_segment_display_2 (
    .g(\n7段译码器译码电路_2_g ), .f(\n7段译码器译码电路_2_f ), .a(\n7段译码器译码电路_2_a ), .b(\n7段译码器译码电路_2_b ),
    .e(\n7段译码器译码电路_2_e ), .d(\n7段译码器译码电路_2_d ), .c(\n7段译码器译码电路_2_c ));  // open: dp
endmodule
