// Logisim project 小型实验室门禁系统电路.circ as structural Verilog: 2 circuits, main circuit main
module main (
  input  \进入 ,
  input  \重置 ,
  input  \离开 ,
  output a1,
  output b1,
  output c1,
  output d1,
  output e1,
  output f1,
  output g1,
  output a0,
  output b0,
  output c0,
  output d0,
  output e0,
  output f0,
  output g0,
  output \报警 
);

  wire and_2_out, and_3_out, and_4_out, main_1_q0, main_1_q1, main_1_q2, main_1_q3, not_1_out, or_1_out,
       \二进制数转8421码电路封装版_1_s1 , \二进制数转8421码电路封装版_1_s2 , \二进制数转8421码电路封装版_1_s4 , \二进制数转8421码电路封装版_1_s8 ,
       \二进制数转8421码电路封装版_1_s10 , \二进制数转8421码电路封装版_1_s20 , \二进制数转8421码电路封装版_1_s40 , \二进制数转8421码电路封装版_1_s80 ;

  and and_1 (\报警 , and_2_out, \进入 );
  \_7段译码器译码电路  \u_7段译码器译码电路_1  (
    .A3(\二进制数转8421码电路封装版_1_s80 ), .A2(\二进制数转8421码电路封装版_1_s40 ), .A1(\二进制数转8421码电路封装版_1_s20 ),
    .A0(\二进制数转8421码电路封装版_1_s10 ), .a(a1), .b(b1), .c(c1), .d(d1), .e(e1), .f(f1), .g(g1));
  and and_2 (and_2_out, main_1_q3, main_1_q2, main_1_q1, main_1_q0);
  not not_1 (not_1_out, and_2_out);
  or or_1 (or_1_out, main_1_q3, main_1_q2, main_1_q1, main_1_q0);
  and and_3 (and_3_out, not_1_out, \进入 );
  and and_4 (and_4_out, \离开 , or_1_out);
  \二进制数转8421码电路封装版  \u_二进制数转8421码电路封装版_1  (
    .S80(\二进制数转8421码电路封装版_1_s80 ), .S40(\二进制数转8421码电路封装版_1_s40 ), .S20(\二进制数转8421码电路封装版_1_s20 ),
    .S10(\二进制数转8421码电路封装版_1_s10 ), .S8(\二进制数转8421码电路封装版_1_s8 ), .S4(\二进制数转8421码电路封装版_1_s4 ),
    .S2(\二进制数转8421码电路封装版_1_s2 ), .S1(\二进制数转8421码电路封装版_1_s1 ), .in_1(main_1_q3), .in_2(main_1_q2),
    .in_3(main_1_q1), .in_4(main_1_q0));
  \四位二进制可逆计数器_main  main_1 (
    .CPD(and_4_out), .Q3(main_1_q3), .Q2(main_1_q2), .Q1(main_1_q1), .Q0(main_1_q0), .\置零 (\重置 ),
    .CPU(and_3_out));
  \_7段译码器译码电路  \u_7段译码器译码电路_2  (
    .A3(\二进制数转8421码电路封装版_1_s8 ), .A2(\二进制数转8421码电路封装版_1_s4 ), .A1(\二进制数转8421码电路封装版_1_s2 ),
    .A0(\二进制数转8421码电路封装版_1_s1 ), .a(a0), .b(b0), .c(c0), .d(d0), .e(e0), .f(f0), .g(g0));
endmodule

module \门禁电路封装版  (
);

  wire main_1_a0, main_1_a1, main_1_b0, main_1_b1, main_1_c0, main_1_c1, main_1_d0, main_1_d1, main_1_e0,
       main_1_e1, main_1_f0, main_1_f1, main_1_g0, main_1_g1, \main_1_报警 , \离开_out , \进入_out , \重置_out ;

  Button \u_进入  (.out(\进入_out ));
  Button \u_重置  (.out(\重置_out ));
  Button \u_离开  (.out(\离开_out ));
  main main_1 (
    .\进入 (\进入_out ), .\重置 (\重置_out ), .\离开 (\离开_out ), .\报警 (\main_1_报警 ), .a1(main_1_a1), .b1(main_1_b1),
    .c1(main_1_c1), .d1(main_1_d1), .e1(main_1_e1), .f1(main_1_f1), .g1(main_1_g1), .a0(main_1_a0),
    .b0(main_1_b0), .c0(main_1_c0), .d0(main_1_d0), .e0(main_1_e0), .f0(main_1_f0), .g0(main_1_g0));
  _7_Segment_Display u_7_segment_display_1 (
    .g(main_1_g1), .f(main_1_f1), .a(main_1_a1), .b(main_1_b1), .e(main_1_e1), .d(main_1_d1), .c(main_1_c1));  // open: dp
  _7_Segment_Display u_7_segment_display_2 (
    .g(main_1_g0), .f(main_1_f0), .a(main_1_a0), .b(main_1_b0), .e(main_1_e0), .d(main_1_d0), .c(main_1_c0));  // open: dp
  LED led_1 (.in(\main_1_报警 ));
endmodule
