// Logisim project 报警电路.circ as structural Verilog: 1 circuit, main circuit main
module main (
  input  \进入 ,
  input  \重置 ,
  input  \离开 ,
  output out_4,
  output out_5,
  output out_6,
  output out_7
);

  wire and_1_out, and_2_out, and_3_out, and_4_out, not_1_out, or_1_out;

  LED \u_警报  (.in(and_1_out));
  and and_1 (and_1_out, and_2_out, \进入 );
  and and_2 (and_2_out, out_4, out_5, out_6, out_7);
  not not_1 (not_1_out, and_2_out);
  or or_1 (or_1_out, out_4, out_5, out_6, out_7);
  and and_3 (and_3_out, not_1_out, \进入 );
  and and_4 (and_4_out, \离开 , or_1_out);
  \四位二进制可逆计数器_main  main_1 (
    .CPD(and_4_out), .Q3(out_4), .Q2(out_5), .Q1(out_6), .Q0(out_7), .\置零 (\重置 ), .CPU(and_3_out));
endmodule
