// Logisim project 实验三设计.circ as structural Verilog: 10 circuits, main circuit 六十进制计数器电路
module \六十进制计数器电路  (
  input  CPU,
  input  Adj,
  input  CPD,
  input  CLR,
  output Q1d,
  output Q1c,
  output Q1b,
  output Q1a,
  output Q0d,
  output Q0c,
  output Q0b,
  output Q0a,
  output _QCC
);

  wire and_1_out, \mod10_1_借位输出 , \mod10_1_进位输出 ;

  and and_1 (and_1_out, Adj, CPD);
  mod10 mod10_1 (
    .CPU(CPU), .CPD(and_1_out), .Q3(Q0d), .Q2(Q0c), .Q1(Q0b), .Q0(Q0a), .\进位输出 (\mod10_1_进位输出 ), .clr(CLR),
    .\借位输出 (\mod10_1_借位输出 ));
  mod6 mod6_1 (
    .CPU(\mod10_1_进位输出 ), .CPD(\mod10_1_借位输出 ), .Q3(Q1d), .Q2(Q1c), .Q1(Q1b), .Q0(Q1a), .\进位输出 (_QCC),
    .clr(CLR));  // open: 借位输出
endmodule

module mod6 (
  input  clr,
  input  CPU,
  input  CPD,
  output Q3,
  output Q2,
  output Q1,
  output Q0,
  output \进位输出 ,
  output \借位输出 
);

  wire and_2_out, and_3_out, and_4_out, and_5_out, and_6_out, and_7_out, D0_qn, D1_qn, D2_qn, D3_qn,
       not_1_out, or_1_out, or_2_out, or_3_out, or_4_out, or_5_out, or_6_out;

  and and_1 (\进位输出 , Q2, Q1);
  or or_1 (or_1_out, Q3, Q2, Q1, Q0);
  or or_2 (or_2_out, \进位输出 , clr);
  or or_3 (or_3_out, and_2_out, and_3_out);
  and and_2 (and_2_out, CPD, D2_qn, or_1_out, D1_qn, D0_qn);
  D_Flip_Flop #(.trigger("falling")) D3 (
    .clk(or_3_out), .D(D3_qn), .Q(Q3), .Qn(D3_qn), .reset(or_2_out));  // open: preset, en
  and and_3 (and_3_out, CPU, Q0, Q1, Q2);
  or or_4 (or_4_out, and_4_out, and_5_out);
  and and_4 (and_4_out, CPD, D1_qn, D0_qn);
  D_Flip_Flop #(.trigger("falling")) D2 (
    .clk(or_4_out), .D(D2_qn), .Q(Q2), .Qn(D2_qn), .reset(or_2_out));  // open: preset, en
  and and_5 (and_5_out, CPU, Q0, Q1);
  or or_5 (or_5_out, and_6_out, and_7_out);
  and and_6 (and_6_out, CPD, or_1_out, D0_qn);
  D_Flip_Flop #(.trigger("falling")) D1 (
    .clk(or_5_out), .D(D1_qn), .Q(Q1), .Qn(D1_qn), .reset(or_2_out));  // open: preset, en
  and and_7 (and_7_out, CPU, Q0);
  or or_6 (or_6_out, CPD, CPU);
  not not_1 (not_1_out, or_1_out);
  D_Flip_Flop #(.trigger("falling")) D0 (
    .clk(or_6_out), .D(D0_qn), .Q(Q0), .Qn(D0_qn), .reset(or_2_out));  // open: preset, en
  and and_8 (\借位输出 , CPD, not_1_out);
endmodule

module mod10 (
  input  clr,
  input  CPU,
  input  CPD,
  output Q3,
  output Q2,
  output Q1,
  output Q0,
  output \进位输出 ,
  output \借位输出 
);

  wire and_2_out, and_3_out, and_4_out, and_5_out, and_6_out, and_7_out, D0_qn, D1_qn, D2_qn, D3_qn,
       not_1_out, or_1_out, or_2_out, or_3_out, or_4_out, or_5_out, or_6_out;

  or or_1 (or_1_out, Q0, Q1, Q2, Q3);
  and and_1 (\进位输出 , Q1, Q3);
  or or_2 (or_2_out, \进位输出 , clr);
  and and_2 (and_2_out, CPD, D2_qn, D1_qn, D0_qn);
  D_Flip_Flop #(.trigger("falling")) D3 (
    .clk(or_3_out), .D(D3_qn), .Q(Q3), .Qn(D3_qn), .reset(or_2_out));  // open: preset, en
  or or_3 (or_3_out, and_2_out, and_3_out);
  and and_3 (and_3_out, CPU, Q0, Q1, Q2);
  and and_4 (and_4_out, CPD, D1_qn, D0_qn, or_1_out);
  D_Flip_Flop #(.trigger("falling")) D2 (
    .clk(or_4_out), .D(D2_qn), .Q(Q2), .Qn(D2_qn), .reset(or_2_out));  // open: preset, en
  or or_4 (or_4_out, and_4_out, and_5_out);
  and and_5 (and_5_out, CPU, Q0, Q1);
  and and_6 (and_6_out, CPD, or_1_out, D0_qn);
  D_Flip_Flop #(.trigger("falling")) D1 (
    .clk(or_5_out), .D(D1_qn), .Q(Q1), .Qn(D1_qn), .reset(or_2_out));  // open: preset, en
  or or_5 (or_5_out, and_6_out, and_7_out);
  and and_7 (and_7_out, CPU, Q0);
  D_Flip_Flop #(.trigger("falling")) D0 (
    .clk(or_6_out), .D(D0_qn), .Q(Q0), .Qn(D0_qn), .reset(or_2_out));  // open: preset, en
  or or_6 (or_6_out, CPD, CPU);
  not not_1 (not_1_out, or_1_out);
  and and_8 (\借位输出 , CPD, not_1_out);
endmodule

module test (
  input  in_1,
  input  in_2,
  input  in_3,
  input  in_4,
  input  in_5,
  output out_6,
  output out_7,
  output out_8,
  output out_9,
  output out_10
);

  wire button_1_out, button_2_out, button_3_out, button_4_out, button_5_out, button_6_out, button_7_out,
       clock_1_out, \n7段译码器译码电路_1_a , \n7段译码器译码电路_1_b , \n7段译码器译码电路_1_c , \n7段译码器译码电路_1_d , \n7段译码器译码电路_1_e ,
       \n7段译码器译码电路_1_f , \n7段译码器译码电路_1_g , \n7段译码器译码电路_2_a , \n7段译码器译码电路_2_b , \n7段译码器译码电路_2_c ,
       \n7段译码器译码电路_2_d , \n7段译码器译码电路_2_e , \n7段译码器译码电路_2_f , \n7段译码器译码电路_2_g , \n7段译码器译码电路_3_a ,
       \n7段译码器译码电路_3_b , \n7段译码器译码电路_3_c , \n7段译码器译码电路_3_d , \n7段译码器译码电路_3_e , \n7段译码器译码电路_3_f ,
       \n7段译码器译码电路_3_g , \n7段译码器译码电路_4_a , \n7段译码器译码电路_4_b , \n7段译码器译码电路_4_c , \n7段译码器译码电路_4_d ,
       \n7段译码器译码电路_4_e , \n7段译码器译码电路_4_f , \n7段译码器译码电路_4_g , \六十进制计数器电路_1_q0a , \六十进制计数器电路_1_q0b ,
       \六十进制计数器电路_1_q0c , \六十进制计数器电路_1_q0d , \六十进制计数器电路_1_q1a , \六十进制计数器电路_1_q1b , \六十进制计数器电路_1_q1c ,
       \六十进制计数器电路_1_q1d , \十二进制计数器或二十四进制的计数器电路_1_out_6 , \十二进制计数器或二十四进制的计数器电路_1_out_7 ,
       \十二进制计数器或二十四进制的计数器电路_1_out_8 , \十二进制计数器或二十四进制的计数器电路_1_out_9 , \十二进制计数器或二十四进制的计数器电路_1_out_10 ,
       \十二进制计数器或二十四进制的计数器电路_1_out_11 , \十二进制计数器或二十四进制的计数器电路_1_out_12 , \十二进制计数器或二十四进制的计数器电路_1_out_13 ,
       \电子钟整点报时电路_1_out_3 ;
  wire [4:0] \显示_上午_或_下午_1_out_3 , \显示_上午_或_下午_1_out_4 , \显示_上午_或_下午_1_out_5 , \显示_上午_或_下午_1_out_6 ;

  T_Flip_Flop t_ff_1 (.clk(out_8), .T(1'b1), .Q(out_6));  // open: Qn, preset, reset, en
  \_7段译码器译码电路  \u_7段译码器译码电路_1  (
    .A3(\六十进制计数器电路_1_q1d ), .A2(\六十进制计数器电路_1_q1c ), .A1(\六十进制计数器电路_1_q1b ), .A0(\六十进制计数器电路_1_q1a ),
    .a(\n7段译码器译码电路_1_a ), .b(\n7段译码器译码电路_1_b ), .c(\n7段译码器译码电路_1_c ), .d(\n7段译码器译码电路_1_d ),
    .e(\n7段译码器译码电路_1_e ), .f(\n7段译码器译码电路_1_f ), .g(\n7段译码器译码电路_1_g ));
  Button button_1 (.out(button_1_out));
  Clock clock_1 (.out(clock_1_out));
  _7_Segment_Display u_7_segment_display_1 (
    .g(\n7段译码器译码电路_1_g ), .f(\n7段译码器译码电路_1_f ), .a(\n7段译码器译码电路_1_a ), .b(\n7段译码器译码电路_1_b ),
    .e(\n7段译码器译码电路_1_e ), .d(\n7段译码器译码电路_1_d ), .c(\n7段译码器译码电路_1_c ));  // open: dp
  \六十进制计数器电路  \u_六十进制计数器电路_1  (
    .CPU(button_2_out), .Adj(in_3), .CPD(button_1_out), ._QCC(out_8), .CLR(button_3_out),
    .Q1d(\六十进制计数器电路_1_q1d ), .Q1c(\六十进制计数器电路_1_q1c ), .Q1b(\六十进制计数器电路_1_q1b ), .Q1a(\六十进制计数器电路_1_q1a ),
    .Q0d(\六十进制计数器电路_1_q0d ), .Q0c(\六十进制计数器电路_1_q0c ), .Q0b(\六十进制计数器电路_1_q0b ), .Q0a(\六十进制计数器电路_1_q0a ));
  \秒计时脉冲产生电路  \u_秒计时脉冲产生电路_1  (.\脉冲输入 (clock_1_out), .\进位输出 (out_10));
  \_7段译码器译码电路  \u_7段译码器译码电路_2  (
    .A3(\六十进制计数器电路_1_q0d ), .A2(\六十进制计数器电路_1_q0c ), .A1(\六十进制计数器电路_1_q0b ), .A0(\六十进制计数器电路_1_q0a ),
    .a(\n7段译码器译码电路_2_a ), .b(\n7段译码器译码电路_2_b ), .c(\n7段译码器译码电路_2_c ), .d(\n7段译码器译码电路_2_d ),
    .e(\n7段译码器译码电路_2_e ), .f(\n7段译码器译码电路_2_f ), .g(\n7段译码器译码电路_2_g ));
  _7_Segment_Display u_7_segment_display_2 (
    .g(\n7段译码器译码电路_2_g ), .f(\n7段译码器译码电路_2_f ), .a(\n7段译码器译码电路_2_a ), .b(\n7段译码器译码电路_2_b ),
    .e(\n7段译码器译码电路_2_e ), .d(\n7段译码器译码电路_2_d ), .c(\n7段译码器译码电路_2_c ));  // open: dp
  Button button_2 (.out(button_2_out));
  Button button_3 (.out(button_3_out));
  Button button_4 (.out(button_4_out));
  \_7段译码器译码电路  \u_7段译码器译码电路_3  (
    .A3(\十二进制计数器或二十四进制的计数器电路_1_out_6 ), .A2(\十二进制计数器或二十四进制的计数器电路_1_out_7 ),
    .A1(\十二进制计数器或二十四进制的计数器电路_1_out_8 ), .A0(\十二进制计数器或二十四进制的计数器电路_1_out_9 ), .a(\n7段译码器译码电路_3_a ),
    .b(\n7段译码器译码电路_3_b ), .c(\n7段译码器译码电路_3_c ), .d(\n7段译码器译码电路_3_d ), .e(\n7段译码器译码电路_3_e ),
    .f(\n7段译码器译码电路_3_f ), .g(\n7段译码器译码电路_3_g ));
  Button button_5 (.out(button_5_out));
  Button button_6 (.out(button_6_out));
  LED led_1 (.in(\电子钟整点报时电路_1_out_3 ));
  \电子钟整点报时电路  \u_电子钟整点报时电路_1  (.START(button_4_out), .out_3(\电子钟整点报时电路_1_out_3 ), .CP(out_10));
  _7_Segment_Display u_7_segment_display_3 (
    .g(\n7段译码器译码电路_3_g ), .f(\n7段译码器译码电路_3_f ), .a(\n7段译码器译码电路_3_a ), .b(\n7段译码器译码电路_3_b ),
    .e(\n7段译码器译码电路_3_e ), .d(\n7段译码器译码电路_3_d ), .c(\n7段译码器译码电路_3_c ));  // open: dp
  \_7段译码器译码电路  \u_7段译码器译码电路_4  (
    .A3(\十二进制计数器或二十四进制的计数器电路_1_out_10 ), .A2(\十二进制计数器或二十四进制的计数器电路_1_out_11 ),
    .A1(\十二进制计数器或二十四进制的计数器电路_1_out_12 ), .A0(\十二进制计数器或二十四进制的计数器电路_1_out_13 ), .a(\n7段译码器译码电路_4_a ),
    .b(\n7段译码器译码电路_4_b ), .c(\n7段译码器译码电路_4_c ), .d(\n7段译码器译码电路_4_d ), .e(\n7段译码器译码电路_4_e ),
    .f(\n7段译码器译码电路_4_f ), .g(\n7段译码器译码电路_4_g ));
  \十二进制计数器或二十四进制的计数器电路  \u_十二进制计数器或二十四进制的计数器电路_1  (
    .Adj(in_4), .CPd(button_6_out), .Set(in_5), .out_14(out_9), .CPu(button_5_out), .CLR(button_7_out),
    .out_6(\十二进制计数器或二十四进制的计数器电路_1_out_6 ), .out_7(\十二进制计数器或二十四进制的计数器电路_1_out_7 ),
    .out_8(\十二进制计数器或二十四进制的计数器电路_1_out_8 ), .out_9(\十二进制计数器或二十四进制的计数器电路_1_out_9 ),
    .out_10(\十二进制计数器或二十四进制的计数器电路_1_out_10 ), .out_11(\十二进制计数器或二十四进制的计数器电路_1_out_11 ),
    .out_12(\十二进制计数器或二十四进制的计数器电路_1_out_12 ), .out_13(\十二进制计数器或二十四进制的计数器电路_1_out_13 ));
  _7_Segment_Display u_7_segment_display_4 (
    .g(\n7段译码器译码电路_4_g ), .f(\n7段译码器译码电路_4_f ), .a(\n7段译码器译码电路_4_a ), .b(\n7段译码器译码电路_4_b ),
    .e(\n7段译码器译码电路_4_e ), .d(\n7段译码器译码电路_4_d ), .c(\n7段译码器译码电路_4_c ));  // open: dp
  Button button_7 (.out(button_7_out));
  T_Flip_Flop t_ff_2 (.clk(out_9), .T(1'b1), .Q(out_7));  // open: Qn, preset, reset, en
  DotMatrix #(.matrixcols(4), .matrixrows(5)) dotmatrix_1 (
    .col0(\显示_上午_或_下午_1_out_3 ), .col1(\显示_上午_或_下午_1_out_4 ), .col2(\显示_上午_或_下午_1_out_5 ),
    .col3(\显示_上午_或_下午_1_out_6 ));
  \显示_上午_或_下午  \u_显示_上午_或_下午_1  (
    .out_3(\显示_上午_或_下午_1_out_3 ), .out_4(\显示_上午_或_下午_1_out_4 ), .out_5(\显示_上午_或_下午_1_out_5 ),
    .out_6(\显示_上午_或_下午_1_out_6 ), .AM_FM(in_1), .TT(in_2));
endmodule

module \显示_上午_或_下午  (
  input  AM_FM,
  input  TT,
  output [4:0] out_3,
  output [4:0] out_4,
  output [4:0] out_5,
  output [4:0] out_6
);

  Multiplexer #(.width(5)) multiplexer_1 (.in0({5{1'b1}}), .in1({5{1'b1}}), .out(out_4), .sel(AM_FM), .en(TT));
  Multiplexer #(.width(5)) multiplexer_2 (.in0(5'b00001), .in1(5'b10000), .out(out_3), .sel(AM_FM), .en(TT));
  Multiplexer #(.width(5)) multiplexer_3 (.in0(5'b00101), .in1(5'b10100), .out(out_5), .sel(AM_FM), .en(TT));
  Multiplexer #(.width(5)) multiplexer_4 (.in0(5'b00001), .in1(5'b10000), .out(out_6), .sel(AM_FM), .en(TT));
endmodule

module \电子钟整点报时电路  (
  input  START,
  input  CP,
  output out_3
);

  wire and_1_out, d_ff_1_q, \mod10_1_进位输出 ;

  D_Flip_Flop d_ff_1 (.clk(START), .D(1'b1), .Q(d_ff_1_q), .reset(\mod10_1_进位输出 ));  // open: Qn, preset, en
  mod10 mod10_1 (
    .CPU(and_1_out), .CPD(1'b0), .Q0(out_3), .\进位输出 (\mod10_1_进位输出 ), .clr(\mod10_1_进位输出 ));  // open: Q3, Q2, Q1, 借位输出
  and and_1 (and_1_out, d_ff_1_q, CP);
endmodule

module \秒计时脉冲产生电路  (
  input  \脉冲输入 ,
  output \进位输出 
);

  wire and_2_out, and_3_out, and_4_out, and_5_out, and_6_out, and_7_out, D0_q, D0_qn, D1_q, D1_qn, D2_q,
       D2_qn, D3_q, D3_qn, nor_1_out, or_1_out, or_2_out, or_3_out, or_4_out;

  and and_1 (\进位输出 , nor_1_out, D3_q);
  nor nor_1 (nor_1_out, D2_q, D1_q, D0_q);
  or or_1 (or_1_out, and_2_out, and_3_out);
  and and_2 (and_2_out, 1'b0, D2_qn, D1_qn, D0_qn);
  D_Flip_Flop #(.trigger("falling")) D3 (
    .clk(or_1_out), .D(D3_qn), .Q(D3_q), .Qn(D3_qn), .reset(\进位输出 ));  // open: preset, en
  and and_3 (and_3_out, \脉冲输入 , D0_q, D1_q, D2_q);
  or or_2 (or_2_out, and_4_out, and_5_out);
  and and_4 (and_4_out, 1'b0, D1_qn, D0_qn);
  D_Flip_Flop #(.trigger("falling")) D2 (
    .clk(or_2_out), .D(D2_qn), .Q(D2_q), .Qn(D2_qn), .reset(\进位输出 ));  // open: preset, en
  and and_5 (and_5_out, \脉冲输入 , D0_q, D1_q);
  or or_3 (or_3_out, and_6_out, and_7_out);
  and and_6 (and_6_out, 1'b0, D0_qn);
  D_Flip_Flop #(.trigger("falling")) D1 (
    .clk(or_3_out), .D(D1_qn), .Q(D1_q), .Qn(D1_qn), .reset(\进位输出 ));  // open: preset, en
  and and_7 (and_7_out, \脉冲输入 , D0_q);
  or or_4 (or_4_out, 1'b0, \脉冲输入 );
  D_Flip_Flop #(.trigger("falling")) D0 (
    .clk(or_4_out), .D(D0_qn), .Q(D0_q), .Qn(D0_qn), .reset(\进位输出 ));  // open: preset, en
endmodule

module \多功能数字钟电路封装  (
  input  in_1,
  input  in_2,
  input  in_3
);

  wire button_1_out, button_2_out, button_3_out, clock_1_out, \多功能数字钟电路_1_out_14 ;
  wire [3:0] \多功能数字钟电路_1_out_8 , \多功能数字钟电路_1_out_9 , \多功能数字钟电路_1_out_10 , \多功能数字钟电路_1_out_11 ,
       \多功能数字钟电路_1_out_12 , \多功能数字钟电路_1_out_13 ;
  wire [4:0] \多功能数字钟电路_1_out_15 , \多功能数字钟电路_1_out_16 , \多功能数字钟电路_1_out_17 , \多功能数字钟电路_1_out_18 ;

  DotMatrix #(.matrixcols(4), .matrixrows(5)) dotmatrix_1 (
    .col0(\多功能数字钟电路_1_out_15 ), .col1(\多功能数字钟电路_1_out_16 ), .col2(\多功能数字钟电路_1_out_17 ),
    .col3(\多功能数字钟电路_1_out_18 ));
  \多功能数字钟电路  \u_多功能数字钟电路_1  (
    .CPu(button_1_out), .Adj1(in_2), .CP(clock_1_out), .CLR(button_3_out), .Adj0(in_1), .Set(in_3),
    .CPd(button_2_out), .out_15(\多功能数字钟电路_1_out_15 ), .out_16(\多功能数字钟电路_1_out_16 ),
    .out_17(\多功能数字钟电路_1_out_17 ), .out_18(\多功能数字钟电路_1_out_18 ), .out_8(\多功能数字钟电路_1_out_8 ),
    .out_9(\多功能数字钟电路_1_out_9 ), .out_10(\多功能数字钟电路_1_out_10 ), .out_11(\多功能数字钟电路_1_out_11 ),
    .out_12(\多功能数字钟电路_1_out_12 ), .out_13(\多功能数字钟电路_1_out_13 ), .out_14(\多功能数字钟电路_1_out_14 ));
  Hex_Digit_Display hex_digit_display_1 (.value(\多功能数字钟电路_1_out_8 ));  // open: dp
  Clock clock_1 (.out(clock_1_out));
  Button button_1 (.out(button_1_out));
  Hex_Digit_Display hex_digit_display_2 (.value(\多功能数字钟电路_1_out_10 ));  // open: dp
  Hex_Digit_Display hex_digit_display_3 (.value(\多功能数字钟电路_1_out_9 ));  // open: dp
  Button button_2 (.out(button_2_out));
  Hex_Digit_Display hex_digit_display_4 (.value(\多功能数字钟电路_1_out_11 ));  // open: dp
  Hex_Digit_Display hex_digit_display_5 (.value(\多功能数字钟电路_1_out_12 ));  // open: dp
  Button button_3 (.out(button_3_out));
  Hex_Digit_Display hex_digit_display_6 (.value(\多功能数字钟电路_1_out_13 ));  // open: dp
  LED led_1 (.in(\多功能数字钟电路_1_out_14 ));
endmodule

module \多功能数字钟电路  (
  input  CPu,
  input  Adj1,
  input  CP,
  input  CLR,
  input  Adj0,
  input  Set,
  input  CPd,
  output [3:0] out_8,
  output [3:0] out_9,
  output [3:0] out_10,
  output [3:0] out_11,
  output [3:0] out_12,
  output [3:0] out_13,
  output out_14,
  output [4:0] out_15,
  output [4:0] out_16,
  output [4:0] out_17,
  output [4:0] out_18
);

  wire _0, and_1_out, and_2_out, and_3_out, and_4_out, and_5_out, and_6_out, and_7_out, and_8_out, and_9_out,
       and_10_out, and_11_out, and_12_out, and_13_out, comparator_1_gt, comparator_2_gt, comparator_3_eq,
       comparator_4_eq, d_ff_1_q, nor_1_out, not_1_out, not_3_out, not_4_out, not_5_out, not_6_out, or_1_out,
       or_2_out, or_3_out, or_4_out, or_5_out, t_ff_1_q, \六十进制计数器电路_1__qcc , \六十进制计数器电路_2__qcc ,
       \十二进制计数器或二十四进制的计数器电路_1_out_14 , \秒计时脉冲产生电路_1_进位输出 ;
  wire [3:0] \十二进制计数器或二十四进制的计数器电路_1_out_9 , \十二进制计数器或二十四进制的计数器电路_1_out_13 ;

  or or_1 (or_1_out, and_1_out, and_4_out, and_2_out);
  and and_1 (and_1_out, \十二进制计数器或二十四进制的计数器电路_1_out_14 , not_1_out);
  not not_1 (not_1_out, Set);
  \显示_上午_或_下午  \u_显示_上午_或_下午_1  (
    .out_3(out_15), .out_4(out_16), .out_5(out_17), .out_6(out_18), .AM_FM(or_2_out), .TT(not_3_out));
  or or_2 (or_2_out, t_ff_1_q, d_ff_1_q);
  T_Flip_Flop t_ff_1 (.clk(or_1_out), .T(1'b1), .Q(t_ff_1_q), .reset(or_3_out));  // open: Qn, preset, en
  or or_3 (or_3_out, CLR, and_3_out);
  and and_2 (and_2_out, not_1_out, and_11_out, nor_1_out, t_ff_1_q);
  not not_2 (_0, d_ff_1_q);
  D_Flip_Flop #(.trigger("falling")) d_ff_1 (.clk(Set), .D(and_5_out), .Q(d_ff_1_q));  // open: Qn, preset, en, reset
  not not_3 (not_3_out, Set);
  nor nor_1 (nor_1_out, \十二进制计数器或二十四进制的计数器电路_1_out_13 [0], \十二进制计数器或二十四进制的计数器电路_1_out_13 [1], \十二进制计数器或二十四进制的计数器电路_1_out_13 [2], \十二进制计数器或二十四进制的计数器电路_1_out_13 [3], \十二进制计数器或二十四进制的计数器电路_1_out_9 [0], \十二进制计数器或二十四进制的计数器电路_1_out_9 [1], \十二进制计数器或二十四进制的计数器电路_1_out_9 [2], \十二进制计数器或二十四进制的计数器电路_1_out_9 [3]);
  and and_3 (and_3_out, _0, Set);
  and and_4 (and_4_out, Set, \十二进制计数器或二十四进制的计数器电路_1_out_14 );
  and and_5 (and_5_out, comparator_1_gt, comparator_2_gt);
  Comparator #(.width(4), .mode("unsigned")) comparator_1 (
    .a(\十二进制计数器或二十四进制的计数器电路_1_out_9 ), .b(4'b0000), .gt(comparator_1_gt));  // open: eq, lt
  Comparator #(.width(4), .mode("unsigned")) comparator_2 (
    .a(\十二进制计数器或二十四进制的计数器电路_1_out_13 ), .b(4'b0001), .gt(comparator_2_gt));  // open: eq, lt
  \十二进制计数器或二十四进制的计数器电路  \u_十二进制计数器或二十四进制的计数器电路_1  (
    .Adj(Adj0), .CPd(and_11_out), .Set(Set), .out_14(\十二进制计数器或二十四进制的计数器电路_1_out_14 ), .CPu(or_4_out),
    .CLR(CLR), .out_6(\十二进制计数器或二十四进制的计数器电路_1_out_9 [3]), .out_7(\十二进制计数器或二十四进制的计数器电路_1_out_9 [2]),
    .out_8(\十二进制计数器或二十四进制的计数器电路_1_out_9 [1]), .out_9(\十二进制计数器或二十四进制的计数器电路_1_out_9 [0]),
    .out_10(\十二进制计数器或二十四进制的计数器电路_1_out_13 [3]), .out_11(\十二进制计数器或二十四进制的计数器电路_1_out_13 [2]),
    .out_12(\十二进制计数器或二十四进制的计数器电路_1_out_13 [1]), .out_13(\十二进制计数器或二十四进制的计数器电路_1_out_13 [0]));
  Multiplexer #(.width(4), .enable("false")) multiplexer_1 (
    .in0(\十二进制计数器或二十四进制的计数器电路_1_out_9 ), .in1(4'b0001), .out(out_8), .sel(and_7_out));
  and and_6 (and_6_out, comparator_3_eq, comparator_4_eq);
  Comparator #(.width(4), .mode("unsigned")) comparator_3 (
    .a(\十二进制计数器或二十四进制的计数器电路_1_out_9 ), .b(\十二进制计数器或二十四进制的计数器电路_1_out_13 ), .eq(comparator_3_eq));  // open: gt, lt
  Comparator #(.width(4), .mode("unsigned")) comparator_4 (
    .a(\十二进制计数器或二十四进制的计数器电路_1_out_9 ), .b(4'b0000), .eq(comparator_4_eq));  // open: gt, lt
  Multiplexer #(.width(4), .enable("false")) multiplexer_2 (
    .in0(\十二进制计数器或二十四进制的计数器电路_1_out_13 ), .in1(4'b0010), .out(out_9), .sel(and_7_out));
  and and_7 (and_7_out, and_6_out, not_4_out);
  not not_4 (not_4_out, Set);
  or or_4 (or_4_out, and_9_out, \六十进制计数器电路_1__qcc );
  \六十进制计数器电路  \u_六十进制计数器电路_1  (
    .CPU(or_5_out), .Adj(Adj0), .CPD(and_10_out), ._QCC(\六十进制计数器电路_1__qcc ), .CLR(CLR), .Q1d(out_10[3]),
    .Q1c(out_10[2]), .Q1b(out_10[1]), .Q1a(out_10[0]), .Q0d(out_11[3]), .Q0c(out_11[2]), .Q0b(out_11[1]),
    .Q0a(out_11[0]));
  or or_5 (or_5_out, \六十进制计数器电路_2__qcc , and_8_out);
  \六十进制计数器电路  \u_六十进制计数器电路_2  (
    .CPU(\秒计时脉冲产生电路_1_进位输出 ), .Adj(1'b0), .CPD(1'b0), ._QCC(\六十进制计数器电路_2__qcc ), .CLR(CLR), .Q1d(out_12[3]),
    .Q1c(out_12[2]), .Q1b(out_12[1]), .Q1a(out_12[0]), .Q0d(out_13[3]), .Q0c(out_13[2]), .Q0b(out_13[1]),
    .Q0a(out_13[0]));
  and and_8 (and_8_out, and_12_out, Adj1);
  and and_9 (and_9_out, and_12_out, not_5_out);
  and and_10 (and_10_out, Adj1, CPd);
  and and_11 (and_11_out, not_6_out, CPd);
  and and_12 (and_12_out, CPu, Adj0);
  not not_5 (not_5_out, Adj1);
  not not_6 (not_6_out, Adj1);
  and and_13 (and_13_out, out_10[2], out_10[0], out_11[3], out_11[0], out_12[2], out_13[3], out_13[0]);
  \电子钟整点报时电路  \u_电子钟整点报时电路_1  (.START(and_13_out), .out_3(out_14), .CP(\秒计时脉冲产生电路_1_进位输出 ));
  \秒计时脉冲产生电路  \u_秒计时脉冲产生电路_1  (.\脉冲输入 (CP), .\进位输出 (\秒计时脉冲产生电路_1_进位输出 ));
endmodule

module \十二进制计数器或二十四进制的计数器电路  (
  input  Set,
  input  CPu,
  input  Adj,
  input  CLR,
  input  CPd,
  output out_6,
  output out_7,
  output out_8,
  output out_9,
  output out_10,
  output out_11,
  output out_12,
  output out_13,
  output out_14
);

  wire and_1_out, and_2_out, and_3_out, and_4_out, and_5_out, comparator_1_gt, not_1_out, or_1_out, or_2_out,
       \六十进制计数器电路_1_q1a , \六十进制计数器电路_1_q1b , \六十进制计数器电路_1_q1c , \六十进制计数器电路_1_q1d ;
  wire [3:0] \六十进制计数器电路_1_q0a ;
  wire [4:0] adder_1_out, adder_2_out, bit_extender_1_out, bit_extender_2_out, bit_extender_3_out,
       divider_1_out, divider_1_rem, multiplier_1_out, multiplier_2_cout, multiplier_2_out, multiplier_3_out,
       subtractor_1_out;

  Subtractor #(.width(5)) subtractor_1 (
    .a(adder_1_out), .b(multiplier_1_out), .out(subtractor_1_out));  // open: bin, bout
  Divider #(.width(5)) divider_1 (
    .a(subtractor_1_out), .b(5'b01010), .out(divider_1_out), .upper({5{1'b0}}), .rem(divider_1_rem));
  Multiplier #(.width(5)) multiplier_1 (
    .a(5'b01100), .b(bit_extender_1_out), .out(multiplier_1_out));  // open: cin, cout
  Multiplexer #(.enable("false")) multiplexer_1 (.in0(1'b0), .in1(\六十进制计数器电路_1_q1d ), .out(out_6), .sel(Set));
  Multiplexer #(.enable("false")) multiplexer_2 (.in0(1'b0), .in1(\六十进制计数器电路_1_q1c ), .out(out_7), .sel(Set));
  Comparator #(.width(5), .mode("unsigned")) comparator_1 (
    .a(adder_1_out), .b(5'b01011), .gt(comparator_1_gt));  // open: eq, lt
  assign bit_extender_1_out = {{4{1'b0}}, comparator_1_gt};  // Bit_Extender bit_extender_1
  Multiplexer #(.enable("false")) multiplexer_3 (
    .in0(divider_1_out[1]), .in1(\六十进制计数器电路_1_q1b ), .out(out_8), .sel(Set));
  Adder #(.width(5)) adder_1 (.a(adder_2_out), .b({1'b0, \六十进制计数器电路_1_q0a }), .out(adder_1_out));  // open: cin, cout
  \六十进制计数器电路  \u_六十进制计数器电路_1  (
    .CPU(CPu), .Adj(Adj), .CPD(and_1_out), .CLR(or_1_out), .Q1d(\六十进制计数器电路_1_q1d ), .Q1c(\六十进制计数器电路_1_q1c ),
    .Q1b(\六十进制计数器电路_1_q1b ), .Q1a(\六十进制计数器电路_1_q1a ), .Q0d(\六十进制计数器电路_1_q0a [3]), .Q0c(\六十进制计数器电路_1_q0a [2]),
    .Q0b(\六十进制计数器电路_1_q0a [1]), .Q0a(\六十进制计数器电路_1_q0a [0]));  // open: _QCC
  and and_1 (and_1_out, CPd, or_2_out);
  Multiplexer #(.enable("false")) multiplexer_4 (
    .in0(divider_1_rem[3]), .in1(\六十进制计数器电路_1_q0a [3]), .out(out_10), .sel(Set));
  Multiplexer #(.enable("false")) multiplexer_5 (
    .in0(divider_1_out[0]), .in1(\六十进制计数器电路_1_q1a ), .out(out_9), .sel(Set));
  Multiplexer #(.enable("false")) multiplexer_6 (
    .in0(divider_1_rem[2]), .in1(\六十进制计数器电路_1_q0a [2]), .out(out_11), .sel(Set));
  Multiplexer #(.enable("false")) multiplexer_7 (
    .in0(divider_1_rem[1]), .in1(\六十进制计数器电路_1_q0a [1]), .out(out_12), .sel(Set));
  Multiplexer #(.enable("false")) multiplexer_8 (
    .in0(divider_1_rem[0]), .in1(\六十进制计数器电路_1_q0a [0]), .out(out_13), .sel(Set));
  assign bit_extender_2_out = {{4{1'b0}}, \六十进制计数器电路_1_q1b };  // Bit_Extender bit_extender_2
  assign bit_extender_3_out = {{4{1'b0}}, \六十进制计数器电路_1_q1a };  // Bit_Extender bit_extender_3
  or or_1 (or_1_out, CLR, and_3_out);
  and and_2 (and_2_out, divider_1_out[0], divider_1_rem[1]);
  or or_2 (or_2_out, \六十进制计数器电路_1_q0a [0], \六十进制计数器电路_1_q0a [1], \六十进制计数器电路_1_q0a [2], \六十进制计数器电路_1_q0a [3], \六十进制计数器电路_1_q1a , \六十进制计数器电路_1_q1b , \六十进制计数器电路_1_q1c , \六十进制计数器电路_1_q1d );
  Multiplier #(.width(5)) multiplier_2 (
    .a(5'b10100), .b(bit_extender_2_out), .out(multiplier_2_out), .cout(multiplier_2_cout));  // open: cin
  Multiplier #(.width(5)) multiplier_3 (
    .a(5'b01010), .b(bit_extender_3_out), .out(multiplier_3_out), .cin(multiplier_2_cout));  // open: cout
  and and_3 (and_3_out, \六十进制计数器电路_1_q1b , \六十进制计数器电路_1_q0a [2]);
  not not_1 (not_1_out, Set);
  and and_4 (and_4_out, not_1_out, and_2_out);
  Adder #(.width(5)) adder_2 (.a(multiplier_2_out), .b(multiplier_3_out), .out(adder_2_out));  // open: cin, cout
  or or_3 (out_14, and_4_out, and_5_out);
  and and_5 (and_5_out, Set, and_3_out);
endmodule
