// Logisim project 乘法器设计.circ as structural Verilog: 3 circuits, main circuit 4×4乘法器设计
module \_4_4乘法器设计  (
  input  [3:0] a_3_0,
  input  [3:0] b_3_0,
  output [7:0] p_7_0
);

  wire [7:0] adder_1_out, adder_2_out, adder_3_out, adder_4_out, bit_extender_1_out, multiplexer_1_out,
       multiplexer_2_out, multiplexer_3_out, shifter_1_out, shifter_2_out, shifter_3_out;

  assign bit_extender_1_out = {{4{1'b0}}, b_3_0};  // Bit_Extender bit_extender_1
  Multiplexer #(.width(8), .enable("false")) multiplexer_1 (
    .in0({8{1'b0}}), .in1(adder_1_out), .out(multiplexer_1_out), .sel(a_3_0[0]));
  Adder adder_1 (.a({8{1'b0}}), .b(bit_extender_1_out), .out(adder_1_out));  // open: cin, cout
  Shifter shifter_1 (.in(bit_extender_1_out), .\dist (3'b001), .out(shifter_1_out));
  Adder adder_2 (.a(multiplexer_1_out), .b(shifter_1_out), .out(adder_2_out));  // open: cin, cout
  Shifter shifter_2 (.in(shifter_1_out), .\dist (3'b001), .out(shifter_2_out));
  Multiplexer #(.width(8), .enable("false")) multiplexer_2 (
    .in0(multiplexer_1_out), .in1(adder_2_out), .out(multiplexer_2_out), .sel(a_3_0[1]));
  Multiplexer #(.width(8), .enable("false")) multiplexer_3 (
    .in0(multiplexer_2_out), .in1(adder_3_out), .out(multiplexer_3_out), .sel(a_3_0[2]));
  Adder adder_3 (.a(multiplexer_2_out), .b(shifter_2_out), .out(adder_3_out));  // open: cin, cout
  Shifter shifter_3 (.in(shifter_2_out), .\dist (3'b001), .out(shifter_3_out));
  Adder adder_4 (.a(multiplexer_3_out), .b(shifter_3_out), .out(adder_4_out));  // open: cin, cout
  Shifter shifter_4 (.in(shifter_3_out), .\dist (3'b001));  // open: out
  Multiplexer #(.width(8), .enable("false")) multiplexer_4 (
    .in0(multiplexer_3_out), .in1(adder_4_out), .out(p_7_0), .sel(a_3_0[3]));
endmodule

module \_32_4乘法器设计  (
  input  [3:0] a_3_0,
  input  [31:0] b_31_0,
  output [31:0] p_32_0
);

  wire [31:0] adder_1_out, adder_2_out, adder_3_out, adder_4_out, multiplexer_1_out, multiplexer_2_out,
       multiplexer_3_out, shifter_1_out, shifter_2_out, shifter_3_out;

  Adder #(.width(32)) adder_1 (.a({32{1'b0}}), .b(b_31_0), .out(adder_1_out));  // open: cin, cout
  Shifter #(.width(32)) shifter_1 (.in(b_31_0), .\dist (5'b00001), .out(shifter_1_out));
  Multiplexer #(.width(32), .enable("false")) multiplexer_1 (
    .in0({32{1'b0}}), .in1(adder_1_out), .out(multiplexer_1_out), .sel(a_3_0[0]));
  Multiplexer #(.width(32), .enable("false")) multiplexer_2 (
    .in0(multiplexer_1_out), .in1(adder_2_out), .out(multiplexer_2_out), .sel(a_3_0[1]));
  Adder #(.width(32)) adder_2 (.a(multiplexer_1_out), .b(shifter_1_out), .out(adder_2_out));  // open: cin, cout
  Shifter #(.width(32)) shifter_2 (.in(shifter_1_out), .\dist (5'b00001), .out(shifter_2_out));
  Adder #(.width(32)) adder_3 (.a(multiplexer_2_out), .b(shifter_2_out), .out(adder_3_out));  // open: cin, cout
  Shifter #(.width(32)) shifter_3 (.in(shifter_2_out), .\dist (5'b00001), .out(shifter_3_out));
  Multiplexer #(.width(32), .enable("false")) multiplexer_3 (
    .in0(multiplexer_2_out), .in1(adder_3_out), .out(multiplexer_3_out), .sel(a_3_0[2]));
  Multiplexer #(.width(32), .enable("false")) multiplexer_4 (
    .in0(multiplexer_3_out), .in1(adder_4_out), .out(p_32_0), .sel(a_3_0[3]));
  Adder #(.width(32)) adder_4 (.a(multiplexer_3_out), .b(shifter_3_out), .out(adder_4_out));  // open: cin, cout
  Shifter #(.width(32)) shifter_4 (.in(shifter_3_out), .\dist (5'b00001));  // open: out
endmodule

module \_32_32乘法器设计  (
  input  [31:0] a_31_0,
  input  [31:0] b_31_0,
  output [31:0] p_31_0
);

  wire [31:0] adder_1_out, adder_2_out, adder_3_out, adder_4_out, adder_5_out, adder_6_out,
       \n32_4乘法器设计_1_p_32_0 , \n32_4乘法器设计_2_p_32_0 , \n32_4乘法器设计_3_p_32_0 , \n32_4乘法器设计_4_p_32_0 ,
       \n32_4乘法器设计_5_p_32_0 , \n32_4乘法器设计_6_p_32_0 , \n32_4乘法器设计_7_p_32_0 , \n32_4乘法器设计_8_p_32_0 ,
       shifter_1_out, shifter_2_out, shifter_3_out, shifter_4_out, shifter_5_out, shifter_6_out,
       shifter_7_out;

  \_32_4乘法器设计  \u_32_4乘法器设计_1  (.a_3_0(a_31_0[3:0]), .b_31_0(b_31_0), .p_32_0(\n32_4乘法器设计_1_p_32_0 ));
  \_32_4乘法器设计  \u_32_4乘法器设计_2  (.a_3_0(a_31_0[7:4]), .b_31_0(b_31_0), .p_32_0(\n32_4乘法器设计_2_p_32_0 ));
  \_32_4乘法器设计  \u_32_4乘法器设计_3  (.a_3_0(a_31_0[11:8]), .b_31_0(b_31_0), .p_32_0(\n32_4乘法器设计_3_p_32_0 ));
  \_32_4乘法器设计  \u_32_4乘法器设计_4  (.a_3_0(a_31_0[15:12]), .b_31_0(b_31_0), .p_32_0(\n32_4乘法器设计_4_p_32_0 ));
  \_32_4乘法器设计  \u_32_4乘法器设计_5  (.a_3_0(a_31_0[19:16]), .b_31_0(b_31_0), .p_32_0(\n32_4乘法器设计_5_p_32_0 ));
  \_32_4乘法器设计  \u_32_4乘法器设计_6  (.a_3_0(a_31_0[23:20]), .b_31_0(b_31_0), .p_32_0(\n32_4乘法器设计_6_p_32_0 ));
  \_32_4乘法器设计  \u_32_4乘法器设计_7  (.a_3_0(a_31_0[27:24]), .b_31_0(b_31_0), .p_32_0(\n32_4乘法器设计_7_p_32_0 ));
  \_32_4乘法器设计  \u_32_4乘法器设计_8  (.a_3_0(a_31_0[31:28]), .b_31_0(b_31_0), .p_32_0(\n32_4乘法器设计_8_p_32_0 ));
  Shifter #(.width(32)) shifter_1 (.in(\n32_4乘法器设计_2_p_32_0 ), .\dist (5'b00100), .out(shifter_1_out));
  Shifter #(.width(32)) shifter_2 (.in(\n32_4乘法器设计_3_p_32_0 ), .\dist (5'b01000), .out(shifter_2_out));
  Shifter #(.width(32)) shifter_3 (.in(\n32_4乘法器设计_4_p_32_0 ), .\dist (5'b01100), .out(shifter_3_out));
  Shifter #(.width(32)) shifter_4 (.in(\n32_4乘法器设计_5_p_32_0 ), .\dist (5'b10000), .out(shifter_4_out));
  Shifter #(.width(32)) shifter_5 (.in(\n32_4乘法器设计_6_p_32_0 ), .\dist (5'b10100), .out(shifter_5_out));
  Shifter #(.width(32)) shifter_6 (.in(\n32_4乘法器设计_7_p_32_0 ), .\dist (5'b11000), .out(shifter_6_out));
  Shifter #(.width(32)) shifter_7 (.in(\n32_4乘法器设计_8_p_32_0 ), .\dist (5'b11100), .out(shifter_7_out));
  Adder #(.width(32)) adder_1 (.a(\n32_4乘法器设计_1_p_32_0 ), .b(shifter_1_out), .out(adder_1_out));  // open: cin, cout
  Adder #(.width(32)) adder_2 (.a(shifter_2_out), .b(shifter_3_out), .out(adder_2_out));  // open: cin, cout
  Adder #(.width(32)) adder_3 (.a(shifter_4_out), .b(shifter_5_out), .out(adder_3_out));  // open: cin, cout
  Adder #(.width(32)) adder_4 (.a(shifter_6_out), .b(shifter_7_out), .out(adder_4_out));  // open: cin, cout
  Adder #(.width(32)) adder_5 (.a(adder_1_out), .b(adder_2_out), .out(adder_5_out));  // open: cin, cout
  Adder #(.width(32)) adder_6 (.a(adder_3_out), .b(adder_4_out), .out(adder_6_out));  // open: cin, cout
  Adder #(.width(32)) adder_7 (.a(adder_5_out), .b(adder_6_out), .out(p_31_0));  // open: cin, cout
endmodule
