// Logisim project 除法器设计.circ as structural Verilog: 5 circuits, main circuit 4位除法单元
module \_4位除法单元  (
  input  [7:0] \被除数 ,
  input  [3:0] \除数 ,
  output [7:0] out_3
);

  wire comparator_1_lt, not_1_out;
  wire [3:0] or_1_out, subtractor_1_out;
  wire [7:0] shifter_1_out;

  Shifter shifter_1 (.in(\被除数 ), .\dist (3'b001), .out(shifter_1_out));
  Comparator #(.width(4), .mode("unsigned")) comparator_1 (
    .a(shifter_1_out[7:4]), .b(\除数 ), .lt(comparator_1_lt));  // open: gt, eq
  not not_1 (not_1_out, comparator_1_lt);
  Subtractor #(.width(4)) subtractor_1 (.a(shifter_1_out[7:4]), .b(\除数 ), .out(subtractor_1_out));  // open: bin, bout
  assign or_1_out = shifter_1_out[3:0] | 4'b0001;  // OR_Gate or_1, 4 bits wide
  Multiplexer #(.width(8), .enable("false")) multiplexer_1 (
    .in0(shifter_1_out), .in1({subtractor_1_out, or_1_out}), .out(out_3), .sel(not_1_out));
endmodule

module \_4_4除法器  (
  input  [3:0] \被除数 ,
  input  [3:0] \除数 ,
  output [3:0] quote,
  output [3:0] rem
);

  wire [7:0] bit_extender_1_out, \n4位除法单元_1_out_3 , \n4位除法单元_2_out_3 , \n4位除法单元_3_out_3 ;

  assign bit_extender_1_out = {{4{1'b0}}, \被除数 };  // Bit_Extender bit_extender_1
  \_4位除法单元  \u_4位除法单元_1  (.\被除数 (bit_extender_1_out), .\除数 (\除数 ), .out_3(\n4位除法单元_1_out_3 ));
  \_4位除法单元  \u_4位除法单元_2  (.\被除数 (\n4位除法单元_1_out_3 ), .\除数 (\除数 ), .out_3(\n4位除法单元_2_out_3 ));
  \_4位除法单元  \u_4位除法单元_3  (.\被除数 (\n4位除法单元_2_out_3 ), .\除数 (\除数 ), .out_3(\n4位除法单元_3_out_3 ));
  \_4位除法单元  \u_4位除法单元_4  (.\被除数 (\n4位除法单元_3_out_3 ), .\除数 (\除数 ), .out_3({rem, quote}));
endmodule

module \_32_32除法器  (
  input  [31:0] \被除数 ,
  input  [31:0] \除数 ,
  output [31:0] \商 ,
  output [31:0] \余数 
);

  wire [31:0] \n32位除法单元_1_d_31_0_2 , \n32位除法单元_1_n1_2 , \n32位除法单元_1_n2_2 , \n32位除法单元_2_d_31_0_2 ,
       \n32位除法单元_2_n1_2 , \n32位除法单元_2_n2_2 , \n32位除法单元_3_d_31_0_2 , \n32位除法单元_3_n1_2 , \n32位除法单元_3_n2_2 ,
       \n32位除法单元_4_d_31_0_2 , \n32位除法单元_4_n1_2 , \n32位除法单元_4_n2_2 , \n32位除法单元_5_d_31_0_2 , \n32位除法单元_5_n1_2 ,
       \n32位除法单元_5_n2_2 , \n32位除法单元_6_d_31_0_2 , \n32位除法单元_6_n1_2 , \n32位除法单元_6_n2_2 , \n32位除法单元_7_d_31_0_2 ,
       \n32位除法单元_7_n1_2 , \n32位除法单元_7_n2_2 , \n32位除法单元_8_d_31_0_2 , \n32位除法单元_8_n1_2 , \n32位除法单元_8_n2_2 ,
       \n32位除法单元_9_d_31_0_2 , \n32位除法单元_9_n1_2 , \n32位除法单元_9_n2_2 , \n32位除法单元_10_d_31_0_2 ,
       \n32位除法单元_10_n1_2 , \n32位除法单元_10_n2_2 , \n32位除法单元_11_d_31_0_2 , \n32位除法单元_11_n1_2 ,
       \n32位除法单元_11_n2_2 , \n32位除法单元_12_d_31_0_2 , \n32位除法单元_12_n1_2 , \n32位除法单元_12_n2_2 ,
       \n32位除法单元_13_d_31_0_2 , \n32位除法单元_13_n1_2 , \n32位除法单元_13_n2_2 , \n32位除法单元_14_d_31_0_2 ,
       \n32位除法单元_14_n1_2 , \n32位除法单元_14_n2_2 , \n32位除法单元_15_d_31_0_2 , \n32位除法单元_15_n1_2 ,
       \n32位除法单元_15_n2_2 , \n32位除法单元_16_d_31_0_2 , \n32位除法单元_16_n1_2 , \n32位除法单元_16_n2_2 ,
       \n32位除法单元_17_d_31_0_2 , \n32位除法单元_17_n1_2 , \n32位除法单元_17_n2_2 , \n32位除法单元_18_d_31_0_2 ,
       \n32位除法单元_18_n1_2 , \n32位除法单元_18_n2_2 , \n32位除法单元_19_d_31_0_2 , \n32位除法单元_19_n1_2 ,
       \n32位除法单元_19_n2_2 , \n32位除法单元_21_d_31_0_2 , \n32位除法单元_21_n1_2 , \n32位除法单元_21_n2_2 ,
       \n32位除法单元_22_d_31_0_2 , \n32位除法单元_22_n1_2 , \n32位除法单元_22_n2_2 , \n32位除法单元_23_d_31_0_2 ,
       \n32位除法单元_23_n1_2 , \n32位除法单元_23_n2_2 , \n32位除法单元_24_d_31_0_2 , \n32位除法单元_24_n1_2 ,
       \n32位除法单元_24_n2_2 , \n32位除法单元_25_d_31_0_2 , \n32位除法单元_25_n1_2 , \n32位除法单元_25_n2_2 ,
       \n32位除法单元_26_d_31_0_2 , \n32位除法单元_26_n1_2 , \n32位除法单元_26_n2_2 , \n32位除法单元_27_d_31_0_2 ,
       \n32位除法单元_27_n1_2 , \n32位除法单元_27_n2_2 , \n32位除法单元_28_d_31_0_2 , \n32位除法单元_28_n1_2 ,
       \n32位除法单元_28_n2_2 , \n32位除法单元_29_d_31_0_2 , \n32位除法单元_29_n1_2 , \n32位除法单元_29_n2_2 ,
       \n32位除法单元_30_d_31_0_2 , \n32位除法单元_30_n1_2 , \n32位除法单元_30_n2_2 , \n32位除法单元_31_d_31_0_2 ,
       \n32位除法单元_31_n1_2 , \n32位除法单元_31_n2_2 , \n32位除法单元_32_d_31_0_2 , \n32位除法单元_32_n1_2 , \n32位除法单元_32_n2_2 ;

  \_32位除法单元  \u_32位除法单元_1  (
    .n2(\被除数 ), .n1({32{1'b0}}), .d_31_0(\除数 ), .n2_2(\n32位除法单元_1_n2_2 ), .n1_2(\n32位除法单元_1_n1_2 ),
    .d_31_0_2(\n32位除法单元_1_d_31_0_2 ));
  \_32位除法单元  \u_32位除法单元_2  (
    .n2(\n32位除法单元_29_n2_2 ), .n1(\n32位除法单元_29_n1_2 ), .d_31_0(\n32位除法单元_29_d_31_0_2 ),
    .n2_2(\n32位除法单元_2_n2_2 ), .n1_2(\n32位除法单元_2_n1_2 ), .d_31_0_2(\n32位除法单元_2_d_31_0_2 ));
  \_32位除法单元  \u_32位除法单元_3  (
    .n2(\n32位除法单元_30_n2_2 ), .n1(\n32位除法单元_30_n1_2 ), .d_31_0(\n32位除法单元_30_d_31_0_2 ),
    .n2_2(\n32位除法单元_3_n2_2 ), .n1_2(\n32位除法单元_3_n1_2 ), .d_31_0_2(\n32位除法单元_3_d_31_0_2 ));
  \_32位除法单元  \u_32位除法单元_4  (
    .n2(\n32位除法单元_31_n2_2 ), .n1(\n32位除法单元_31_n1_2 ), .d_31_0(\n32位除法单元_31_d_31_0_2 ),
    .n2_2(\n32位除法单元_4_n2_2 ), .n1_2(\n32位除法单元_4_n1_2 ), .d_31_0_2(\n32位除法单元_4_d_31_0_2 ));
  \_32位除法单元  \u_32位除法单元_5  (
    .n2(\n32位除法单元_32_n2_2 ), .n1(\n32位除法单元_32_n1_2 ), .d_31_0(\n32位除法单元_32_d_31_0_2 ),
    .n2_2(\n32位除法单元_5_n2_2 ), .n1_2(\n32位除法单元_5_n1_2 ), .d_31_0_2(\n32位除法单元_5_d_31_0_2 ));
  \_32位除法单元  \u_32位除法单元_6  (
    .n2(\n32位除法单元_1_n2_2 ), .n1(\n32位除法单元_1_n1_2 ), .d_31_0(\n32位除法单元_1_d_31_0_2 ), .n2_2(\n32位除法单元_6_n2_2 ),
    .n1_2(\n32位除法单元_6_n1_2 ), .d_31_0_2(\n32位除法单元_6_d_31_0_2 ));
  \_32位除法单元  \u_32位除法单元_7  (
    .n2(\n32位除法单元_2_n2_2 ), .n1(\n32位除法单元_2_n1_2 ), .d_31_0(\n32位除法单元_2_d_31_0_2 ), .n2_2(\n32位除法单元_7_n2_2 ),
    .n1_2(\n32位除法单元_7_n1_2 ), .d_31_0_2(\n32位除法单元_7_d_31_0_2 ));
  \_32位除法单元  \u_32位除法单元_8  (
    .n2(\n32位除法单元_3_n2_2 ), .n1(\n32位除法单元_3_n1_2 ), .d_31_0(\n32位除法单元_3_d_31_0_2 ), .n2_2(\n32位除法单元_8_n2_2 ),
    .n1_2(\n32位除法单元_8_n1_2 ), .d_31_0_2(\n32位除法单元_8_d_31_0_2 ));
  \_32位除法单元  \u_32位除法单元_9  (
    .n2(\n32位除法单元_4_n2_2 ), .n1(\n32位除法单元_4_n1_2 ), .d_31_0(\n32位除法单元_4_d_31_0_2 ), .n2_2(\n32位除法单元_9_n2_2 ),
    .n1_2(\n32位除法单元_9_n1_2 ), .d_31_0_2(\n32位除法单元_9_d_31_0_2 ));
  \_32位除法单元  \u_32位除法单元_10  (
    .n2(\n32位除法单元_5_n2_2 ), .n1(\n32位除法单元_5_n1_2 ), .d_31_0(\n32位除法单元_5_d_31_0_2 ),
    .n2_2(\n32位除法单元_10_n2_2 ), .n1_2(\n32位除法单元_10_n1_2 ), .d_31_0_2(\n32位除法单元_10_d_31_0_2 ));
  \_32位除法单元  \u_32位除法单元_11  (
    .n2(\n32位除法单元_6_n2_2 ), .n1(\n32位除法单元_6_n1_2 ), .d_31_0(\n32位除法单元_6_d_31_0_2 ),
    .n2_2(\n32位除法单元_11_n2_2 ), .n1_2(\n32位除法单元_11_n1_2 ), .d_31_0_2(\n32位除法单元_11_d_31_0_2 ));
  \_32位除法单元  \u_32位除法单元_12  (
    .n2(\n32位除法单元_7_n2_2 ), .n1(\n32位除法单元_7_n1_2 ), .d_31_0(\n32位除法单元_7_d_31_0_2 ),
    .n2_2(\n32位除法单元_12_n2_2 ), .n1_2(\n32位除法单元_12_n1_2 ), .d_31_0_2(\n32位除法单元_12_d_31_0_2 ));
  \_32位除法单元  \u_32位除法单元_13  (
    .n2(\n32位除法单元_8_n2_2 ), .n1(\n32位除法单元_8_n1_2 ), .d_31_0(\n32位除法单元_8_d_31_0_2 ),
    .n2_2(\n32位除法单元_13_n2_2 ), .n1_2(\n32位除法单元_13_n1_2 ), .d_31_0_2(\n32位除法单元_13_d_31_0_2 ));
  \_32位除法单元  \u_32位除法单元_14  (
    .n2(\n32位除法单元_9_n2_2 ), .n1(\n32位除法单元_9_n1_2 ), .d_31_0(\n32位除法单元_9_d_31_0_2 ),
    .n2_2(\n32位除法单元_14_n2_2 ), .n1_2(\n32位除法单元_14_n1_2 ), .d_31_0_2(\n32位除法单元_14_d_31_0_2 ));
  \_32位除法单元  \u_32位除法单元_15  (
    .n2(\n32位除法单元_10_n2_2 ), .n1(\n32位除法单元_10_n1_2 ), .d_31_0(\n32位除法单元_10_d_31_0_2 ),
    .n2_2(\n32位除法单元_15_n2_2 ), .n1_2(\n32位除法单元_15_n1_2 ), .d_31_0_2(\n32位除法单元_15_d_31_0_2 ));
  \_32位除法单元  \u_32位除法单元_16  (
    .n2(\n32位除法单元_11_n2_2 ), .n1(\n32位除法单元_11_n1_2 ), .d_31_0(\n32位除法单元_11_d_31_0_2 ),
    .n2_2(\n32位除法单元_16_n2_2 ), .n1_2(\n32位除法单元_16_n1_2 ), .d_31_0_2(\n32位除法单元_16_d_31_0_2 ));
  \_32位除法单元  \u_32位除法单元_17  (
    .n2(\n32位除法单元_12_n2_2 ), .n1(\n32位除法单元_12_n1_2 ), .d_31_0(\n32位除法单元_12_d_31_0_2 ),
    .n2_2(\n32位除法单元_17_n2_2 ), .n1_2(\n32位除法单元_17_n1_2 ), .d_31_0_2(\n32位除法单元_17_d_31_0_2 ));
  \_32位除法单元  \u_32位除法单元_18  (
    .n2(\n32位除法单元_13_n2_2 ), .n1(\n32位除法单元_13_n1_2 ), .d_31_0(\n32位除法单元_13_d_31_0_2 ),
    .n2_2(\n32位除法单元_18_n2_2 ), .n1_2(\n32位除法单元_18_n1_2 ), .d_31_0_2(\n32位除法单元_18_d_31_0_2 ));
  \_32位除法单元  \u_32位除法单元_19  (
    .n2(\n32位除法单元_14_n2_2 ), .n1(\n32位除法单元_14_n1_2 ), .d_31_0(\n32位除法单元_14_d_31_0_2 ),
    .n2_2(\n32位除法单元_19_n2_2 ), .n1_2(\n32位除法单元_19_n1_2 ), .d_31_0_2(\n32位除法单元_19_d_31_0_2 ));
  \_32位除法单元  \u_32位除法单元_20  (
    .n2(\n32位除法单元_15_n2_2 ), .n1(\n32位除法单元_15_n1_2 ), .d_31_0(\n32位除法单元_15_d_31_0_2 ), .n2_2(\商 ), .n1_2(\余数 ));  // open: d_31_0_2
  \_32位除法单元  \u_32位除法单元_21  (
    .n2(\n32位除法单元_16_n2_2 ), .n1(\n32位除法单元_16_n1_2 ), .d_31_0(\n32位除法单元_16_d_31_0_2 ),
    .n2_2(\n32位除法单元_21_n2_2 ), .n1_2(\n32位除法单元_21_n1_2 ), .d_31_0_2(\n32位除法单元_21_d_31_0_2 ));
  \_32位除法单元  \u_32位除法单元_22  (
    .n2(\n32位除法单元_17_n2_2 ), .n1(\n32位除法单元_17_n1_2 ), .d_31_0(\n32位除法单元_17_d_31_0_2 ),
    .n2_2(\n32位除法单元_22_n2_2 ), .n1_2(\n32位除法单元_22_n1_2 ), .d_31_0_2(\n32位除法单元_22_d_31_0_2 ));
  \_32位除法单元  \u_32位除法单元_23  (
    .n2(\n32位除法单元_18_n2_2 ), .n1(\n32位除法单元_18_n1_2 ), .d_31_0(\n32位除法单元_18_d_31_0_2 ),
    .n2_2(\n32位除法单元_23_n2_2 ), .n1_2(\n32位除法单元_23_n1_2 ), .d_31_0_2(\n32位除法单元_23_d_31_0_2 ));
  \_32位除法单元  \u_32位除法单元_24  (
    .n2(\n32位除法单元_19_n2_2 ), .n1(\n32位除法单元_19_n1_2 ), .d_31_0(\n32位除法单元_19_d_31_0_2 ),
    .n2_2(\n32位除法单元_24_n2_2 ), .n1_2(\n32位除法单元_24_n1_2 ), .d_31_0_2(\n32位除法单元_24_d_31_0_2 ));
  \_32位除法单元  \u_32位除法单元_25  (
    .n2(\n32位除法单元_21_n2_2 ), .n1(\n32位除法单元_21_n1_2 ), .d_31_0(\n32位除法单元_21_d_31_0_2 ),
    .n2_2(\n32位除法单元_25_n2_2 ), .n1_2(\n32位除法单元_25_n1_2 ), .d_31_0_2(\n32位除法单元_25_d_31_0_2 ));
  \_32位除法单元  \u_32位除法单元_26  (
    .n2(\n32位除法单元_22_n2_2 ), .n1(\n32位除法单元_22_n1_2 ), .d_31_0(\n32位除法单元_22_d_31_0_2 ),
    .n2_2(\n32位除法单元_26_n2_2 ), .n1_2(\n32位除法单元_26_n1_2 ), .d_31_0_2(\n32位除法单元_26_d_31_0_2 ));
  \_32位除法单元  \u_32位除法单元_27  (
    .n2(\n32位除法单元_23_n2_2 ), .n1(\n32位除法单元_23_n1_2 ), .d_31_0(\n32位除法单元_23_d_31_0_2 ),
    .n2_2(\n32位除法单元_27_n2_2 ), .n1_2(\n32位除法单元_27_n1_2 ), .d_31_0_2(\n32位除法单元_27_d_31_0_2 ));
  \_32位除法单元  \u_32位除法单元_28  (
    .n2(\n32位除法单元_24_n2_2 ), .n1(\n32位除法单元_24_n1_2 ), .d_31_0(\n32位除法单元_24_d_31_0_2 ),
    .n2_2(\n32位除法单元_28_n2_2 ), .n1_2(\n32位除法单元_28_n1_2 ), .d_31_0_2(\n32位除法单元_28_d_31_0_2 ));
  \_32位除法单元  \u_32位除法单元_29  (
    .n2(\n32位除法单元_25_n2_2 ), .n1(\n32位除法单元_25_n1_2 ), .d_31_0(\n32位除法单元_25_d_31_0_2 ),
    .n2_2(\n32位除法单元_29_n2_2 ), .n1_2(\n32位除法单元_29_n1_2 ), .d_31_0_2(\n32位除法单元_29_d_31_0_2 ));
  \_32位除法单元  \u_32位除法单元_30  (
    .n2(\n32位除法单元_26_n2_2 ), .n1(\n32位除法单元_26_n1_2 ), .d_31_0(\n32位除法单元_26_d_31_0_2 ),
    .n2_2(\n32位除法单元_30_n2_2 ), .n1_2(\n32位除法单元_30_n1_2 ), .d_31_0_2(\n32位除法单元_30_d_31_0_2 ));
  \_32位除法单元  \u_32位除法单元_31  (
    .n2(\n32位除法单元_27_n2_2 ), .n1(\n32位除法单元_27_n1_2 ), .d_31_0(\n32位除法单元_27_d_31_0_2 ),
    .n2_2(\n32位除法单元_31_n2_2 ), .n1_2(\n32位除法单元_31_n1_2 ), .d_31_0_2(\n32位除法单元_31_d_31_0_2 ));
  \_32位除法单元  \u_32位除法单元_32  (
    .n2(\n32位除法单元_28_n2_2 ), .n1(\n32位除法单元_28_n1_2 ), .d_31_0(\n32位除法单元_28_d_31_0_2 ),
    .n2_2(\n32位除法单元_32_n2_2 ), .n1_2(\n32位除法单元_32_n1_2 ), .d_31_0_2(\n32位除法单元_32_d_31_0_2 ));
endmodule

module \_32位除法单元  (
  input  [31:0] n2,
  input  [31:0] n1,
  input  [31:0] d_31_0,
  output [31:0] n2_2,
  output [31:0] n1_2,
  output [31:0] d_31_0_2
);

  wire comparator_1_lt, not_1_out;
  wire [31:0] or_1_out, subtractor_1_out;

  Comparator #(.width(32), .mode("unsigned")) comparator_1 (
    .a({n1[30:0], n2[31]}), .b(d_31_0), .lt(comparator_1_lt));  // open: gt, eq
  Subtractor #(.width(32)) subtractor_1 (
    .a({n1[30:0], n2[31]}), .b(d_31_0), .out(subtractor_1_out));  // open: bin, bout
  assign or_1_out = {n2[30:0], 1'b0} | 32'h1;  // OR_Gate or_1, 32 bits wide
  not not_1 (not_1_out, comparator_1_lt);
  Multiplexer #(.width(32), .enable("false")) multiplexer_1 (
    .in0({n2[30:0], 1'b0}), .in1(or_1_out), .out(n2_2), .sel(not_1_out));
  Multiplexer #(.width(32), .enable("false")) multiplexer_2 (
    .in0({n1[30:0], n2[31]}), .in1(subtractor_1_out), .out(n1_2), .sel(not_1_out));

  assign d_31_0_2 = d_31_0;
endmodule

module \封装  (
  input  [31:0] in_1,
  input  [31:0] in_2,
  output [31:0] out_3,
  output [31:0] out_4
);

  \_32_32除法器  \u_32_32除法器_1  (.\被除数 (in_1), .\除数 (in_2), .\商 (out_3), .\余数 (out_4));
endmodule
