// Logisim project Fibo111.circ as structural Verilog: 1 circuit, main circuit main
module main (
  input  start,
  input  clr,
  input  clk,
  input  n_i_1,
  output [31:0] out_5
);

  wire and_1_out, not_1_out;
  wire [31:0] multiplexer_1_out, multiplexer_2_out, multiplexer_3_out, multiplexer_4_out, multiplexer_5_out,
       multiplexer_6_out, multiplexer_7_out, multiplexer_8_out, register_1_q, register_3_q, register_4_q,
       undriven, undriven_2, undriven_3, undriven_4, undriven_5, undriven_6, undriven_7, undriven_8;

  and and_1 (and_1_out, start, not_1_out);
  not not_1 (not_1_out, clr);
  Multiplexer #(.width(32), .enable("false")) multiplexer_1 (
    .in0({32{1'b0}}), .in1(multiplexer_5_out), .out(multiplexer_1_out), .sel(and_1_out));
  Register #(.width(32), .trigger("falling")) register_1 (
    .D(multiplexer_1_out), .Q(register_1_q), .clk(clk));  // open: en, clr
  Register #(.width(32), .trigger("falling")) register_2 (
    .D(multiplexer_2_out), .Q(out_5), .clk(clk));  // open: en, clr
  Multiplexer #(.width(32), .enable("false")) multiplexer_2 (
    .in0(32'h1), .in1(multiplexer_6_out), .out(multiplexer_2_out), .sel(and_1_out));
  Register #(.width(32), .trigger("falling")) register_3 (
    .D(multiplexer_3_out), .Q(register_3_q), .clk(clk));  // open: en, clr
  Multiplexer #(.width(32), .enable("false")) multiplexer_3 (
    .in0(32'h1), .in1(multiplexer_7_out), .out(multiplexer_3_out), .sel(and_1_out));
  Multiplexer #(.width(32), .enable("false")) multiplexer_4 (
    .in0(32'h1), .in1(multiplexer_8_out), .out(multiplexer_4_out), .sel(and_1_out));
  Register #(.width(32), .trigger("falling")) register_4 (
    .D(multiplexer_4_out), .Q(register_4_q), .clk(clk));  // open: en, clr
  Multiplexer #(.width(32), .enable("false")) multiplexer_5 (
    .in0(undriven), .in1(undriven_6), .out(multiplexer_5_out), .sel(n_i_1));
  Multiplexer #(.width(32), .enable("false")) multiplexer_6 (
    .in0(undriven_2), .in1(undriven_7), .out(multiplexer_6_out), .sel(n_i_1));
  Multiplexer #(.width(32), .enable("false")) multiplexer_7 (
    .in0(undriven_3), .in1(undriven_8), .out(multiplexer_7_out), .sel(n_i_1));
  Multiplexer #(.width(32), .enable("false")) multiplexer_8 (
    .in0(undriven_4), .in1(undriven_5), .out(multiplexer_8_out), .sel(n_i_1));
endmodule
