// Logisim project 斐波拉契数列.circ as structural Verilog: 6 circuits, main circuit sqrX
module sqrX (
  input  [31:0] a,
  input  [31:0] b,
  input  [31:0] c,
  input  [31:0] d,
  output [31:0] a2_bc,
  output [31:0] ab_bd,
  output [31:0] ac_cd,
  output [31:0] bc_d2
);

  wire [31:0] multiplier_1_out, multiplier_2_out, multiplier_3_out, multiplier_4_out, multiplier_5_out,
       multiplier_6_out, multiplier_7_out;

  Multiplier #(.width(32)) multiplier_1 (.a(a), .b(a), .out(multiplier_1_out));  // open: cin, cout
  Multiplier #(.width(32)) multiplier_2 (.a(a), .b(b), .out(multiplier_2_out));  // open: cin, cout
  Multiplier #(.width(32)) multiplier_3 (.a(a), .b(c), .out(multiplier_3_out));  // open: cin, cout
  Multiplier #(.width(32)) multiplier_4 (.a(b), .b(c), .out(multiplier_4_out));  // open: cin, cout
  Multiplier #(.width(32)) multiplier_5 (.a(b), .b(d), .out(multiplier_5_out));  // open: cin, cout
  Multiplier #(.width(32)) multiplier_6 (.a(c), .b(d), .out(multiplier_6_out));  // open: cin, cout
  Multiplier #(.width(32)) multiplier_7 (.a(d), .b(d), .out(multiplier_7_out));  // open: cin, cout
  Adder #(.width(32)) adder_1 (.a(multiplier_1_out), .b(multiplier_4_out), .out(a2_bc));  // open: cin, cout
  Adder #(.width(32)) adder_2 (.a(multiplier_2_out), .b(multiplier_5_out), .out(ab_bd));  // open: cin, cout
  Adder #(.width(32)) adder_3 (.a(multiplier_3_out), .b(multiplier_6_out), .out(ac_cd));  // open: cin, cout
  Adder #(.width(32)) adder_4 (.a(multiplier_4_out), .b(multiplier_7_out), .out(bc_d2));  // open: cin, cout
endmodule

module sqrX_A (
  input  [31:0] a,
  input  [31:0] b,
  input  [31:0] c,
  input  [31:0] d,
  output [31:0] ab_bd,
  output [31:0] a2_bc_ab_bd,
  output [31:0] bc_d2,
  output [31:0] ac_cd_bc_d2
);

  wire [31:0] adder_2_out, adder_4_out, multiplier_1_out, multiplier_2_out, multiplier_3_out,
       multiplier_4_out, multiplier_5_out, multiplier_6_out, multiplier_7_out;

  Multiplier #(.width(32)) multiplier_1 (.a(a), .b(a), .out(multiplier_1_out));  // open: cin, cout
  Multiplier #(.width(32)) multiplier_2 (.a(a), .b(b), .out(multiplier_2_out));  // open: cin, cout
  Multiplier #(.width(32)) multiplier_3 (.a(a), .b(c), .out(multiplier_3_out));  // open: cin, cout
  Multiplier #(.width(32)) multiplier_4 (.a(b), .b(c), .out(multiplier_4_out));  // open: cin, cout
  Multiplier #(.width(32)) multiplier_5 (.a(b), .b(d), .out(multiplier_5_out));  // open: cin, cout
  Multiplier #(.width(32)) multiplier_6 (.a(c), .b(d), .out(multiplier_6_out));  // open: cin, cout
  Multiplier #(.width(32)) multiplier_7 (.a(d), .b(d), .out(multiplier_7_out));  // open: cin, cout
  Adder #(.width(32)) adder_1 (.a(multiplier_2_out), .b(multiplier_5_out), .out(ab_bd));  // open: cin, cout
  Adder #(.width(32)) adder_2 (.a(multiplier_1_out), .b(multiplier_4_out), .out(adder_2_out));  // open: cin, cout
  Adder #(.width(32)) adder_3 (.a(multiplier_4_out), .b(multiplier_7_out), .out(bc_d2));  // open: cin, cout
  Adder #(.width(32)) adder_4 (.a(multiplier_3_out), .b(multiplier_6_out), .out(adder_4_out));  // open: cin, cout
  Adder #(.width(32)) adder_5 (.a(ab_bd), .b(adder_2_out), .out(a2_bc_ab_bd));  // open: cin, cout
  Adder #(.width(32)) adder_6 (.a(bc_d2), .b(adder_4_out), .out(ac_cd_bc_d2));  // open: cin, cout
endmodule

module Display (
  input  [31:0] in_1,
  output [3:0] out_2,
  output [3:0] out_3,
  output [3:0] out_4,
  output [3:0] out_5,
  output [3:0] out_6,
  output [3:0] out_7,
  output [3:0] out_8,
  output [3:0] out_9,
  output [3:0] out_10,
  output [3:0] out_11
);

  wire [31:0] divider_1_out, divider_1_rem, divider_2_out, divider_2_rem, divider_3_out, divider_3_rem,
       divider_4_out, divider_4_rem, divider_5_out, divider_5_rem, divider_6_out, divider_6_rem,
       divider_7_out, divider_7_rem, divider_8_out, divider_8_rem, divider_9_out, divider_9_rem;

  BitSelector #(.width(32), .group(4)) bitselector_1 (.in(divider_1_rem), .out(out_2), .sel(3'b000));
  Divider #(.width(32)) divider_1 (.a(in_1), .b(32'ha), .out(divider_1_out), .upper({32{1'b0}}), .rem(divider_1_rem));
  BitSelector #(.width(32), .group(4)) bitselector_2 (.in(divider_2_rem), .out(out_3), .sel(3'b000));
  Divider #(.width(32)) divider_2 (
    .a(divider_1_out), .b(32'ha), .out(divider_2_out), .rem(divider_2_rem));  // open: upper
  BitSelector #(.width(32), .group(4)) bitselector_3 (.in(divider_3_rem), .out(out_4), .sel(3'b000));
  Divider #(.width(32)) divider_3 (
    .a(divider_2_out), .b(32'ha), .out(divider_3_out), .rem(divider_3_rem));  // open: upper
  BitSelector #(.width(32), .group(4)) bitselector_4 (.in(divider_4_rem), .out(out_5), .sel(3'b000));
  Divider #(.width(32)) divider_4 (
    .a(divider_3_out), .b(32'ha), .out(divider_4_out), .rem(divider_4_rem));  // open: upper
  BitSelector #(.width(32), .group(4)) bitselector_5 (.in(divider_5_rem), .out(out_6), .sel(3'b000));
  Divider #(.width(32)) divider_5 (
    .a(divider_4_out), .b(32'ha), .out(divider_5_out), .rem(divider_5_rem));  // open: upper
  BitSelector #(.width(32), .group(4)) bitselector_6 (.in(divider_6_rem), .out(out_7), .sel(3'b000));
  Divider #(.width(32)) divider_6 (
    .a(divider_5_out), .b(32'ha), .out(divider_6_out), .rem(divider_6_rem));  // open: upper
  BitSelector #(.width(32), .group(4)) bitselector_7 (.in(divider_7_rem), .out(out_8), .sel(3'b000));
  Divider #(.width(32)) divider_7 (
    .a(divider_6_out), .b(32'ha), .out(divider_7_out), .rem(divider_7_rem));  // open: upper
  BitSelector #(.width(32), .group(4)) bitselector_8 (.in(divider_8_rem), .out(out_9), .sel(3'b000));
  Divider #(.width(32)) divider_8 (
    .a(divider_7_out), .b(32'ha), .out(divider_8_out), .rem(divider_8_rem));  // open: upper
  BitSelector #(.width(32), .group(4)) bitselector_9 (.in(divider_9_rem), .out(out_10), .sel(3'b000));
  Divider #(.width(32)) divider_9 (
    .a(divider_8_out), .b(32'ha), .out(divider_9_out), .rem(divider_9_rem));  // open: upper
  BitSelector #(.width(32), .group(4)) bitselector_10 (.in(divider_9_out), .out(out_11), .sel(3'b000));
endmodule

module Controller (
  input  [5:0] n,
  input  clear,
  input  clk,
  output ni_1,
  output start,
  output clk_2,
  output clear_2
);

  wire comparator_1_gt, not_1_out, not_2_out, or_1_out, or_2_out;
  wire [7:0] counter_1_q;

  not not_1 (not_1_out, clear);
  or or_1 (or_1_out, clk, clear);
  Shift_Register #(.length(6)) shift_register_1 (
    .shift(not_1_out), .in(1'b0), .clk(or_1_out), .out(ni_1), .load(clear), .d0(n[0]), .d1(n[1]), .d2(n[2]),
    .d3(n[3]), .d4(n[4]), .d5(n[5]));  // open: clr, q0, q1, q2, q3, q4, q5
  or or_2 (or_2_out, start, ni_1);
  Counter counter_1 (.load(1'b0), .D({8{1'b0}}), .count(1'b1), .Q(counter_1_q), .clk(clk), .clr(clear));  // open: carry
  D_Flip_Flop d_ff_1 (.clk(or_1_out), .D(or_2_out), .Q(start), .reset(clear));  // open: Qn, preset, en
  not not_2 (not_2_out, comparator_1_gt);
  Comparator #(.mode("unsigned")) comparator_1 (.a(counter_1_q), .b(8'h5), .gt(comparator_1_gt));  // open: eq, lt
  and and_1 (clk_2, clk, not_2_out);

  assign clear_2 = clear;
endmodule

module main (
  input  [5:0] in_1
);

  wire button_1_out, button_2_out, controller_1_clear_2, controller_1_clk_2, controller_1_ni_1,
       controller_1_start;
  wire [3:0] display_1_out_2, display_1_out_3, display_1_out_4, display_1_out_5, display_1_out_6,
       display_1_out_7, display_1_out_8, display_1_out_9, display_1_out_10, display_1_out_11;
  wire [31:0] fibo_1_out_5;

  Controller controller_1 (
    .n(in_1), .start(controller_1_start), .ni_1(controller_1_ni_1), .clk_2(controller_1_clk_2),
    .clear_2(controller_1_clear_2), .clear(button_1_out), .clk(button_2_out));
  Button button_1 (.out(button_1_out));
  Button button_2 (.out(button_2_out));
  Fibo fibo_1 (
    .start(controller_1_start), .clr(controller_1_clear_2), .clk(controller_1_clk_2),
    .n_i_1(controller_1_ni_1), .out_5(fibo_1_out_5));
  Hex_Digit_Display hex_digit_display_1 (.value(display_1_out_10));  // open: dp
  Hex_Digit_Display hex_digit_display_2 (.value(display_1_out_11));  // open: dp
  Display display_1 (
    .in_1(fibo_1_out_5), .out_2(display_1_out_2), .out_3(display_1_out_3), .out_4(display_1_out_4),
    .out_5(display_1_out_5), .out_6(display_1_out_6), .out_7(display_1_out_7), .out_8(display_1_out_8),
    .out_9(display_1_out_9), .out_10(display_1_out_10), .out_11(display_1_out_11));
  Hex_Digit_Display hex_digit_display_3 (.value(display_1_out_8));  // open: dp
  Hex_Digit_Display hex_digit_display_4 (.value(display_1_out_9));  // open: dp
  Hex_Digit_Display hex_digit_display_5 (.value(display_1_out_7));  // open: dp
  Hex_Digit_Display hex_digit_display_6 (.value(display_1_out_6));  // open: dp
  Hex_Digit_Display hex_digit_display_7 (.value(display_1_out_4));  // open: dp
  Hex_Digit_Display hex_digit_display_8 (.value(display_1_out_5));  // open: dp
  Hex_Digit_Display hex_digit_display_9 (.value(display_1_out_2));  // open: dp
  Hex_Digit_Display hex_digit_display_10 (.value(display_1_out_3));  // open: dp
endmodule

module Fibo (
  input  start,
  input  clk,
  input  n_i_1,
  input  clr,
  output [31:0] out_5
);

  wire [31:0] multiplexer_1_out, multiplexer_2_out, multiplexer_3_out, multiplexer_4_out, multiplexer_5_out,
       multiplexer_6_out, multiplexer_7_out, multiplexer_8_out, register_1_q, register_3_q, register_4_q,
       sqrx_1_a2_bc, sqrx_1_ab_bd, sqrx_1_ac_cd, sqrx_1_bc_d2, sqrx_a_1_a2_bc_ab_bd, sqrx_a_1_ab_bd,
       sqrx_a_1_ac_cd_bc_d2, sqrx_a_1_bc_d2;

  Multiplexer #(.width(32), .enable("false")) multiplexer_1 (
    .in0({32{1'b0}}), .in1(multiplexer_5_out), .out(multiplexer_1_out), .sel(start));
  Multiplexer #(.width(32), .enable("false")) multiplexer_2 (
    .in0(32'h1), .in1(multiplexer_6_out), .out(multiplexer_2_out), .sel(start));
  Multiplexer #(.width(32), .enable("false")) multiplexer_3 (
    .in0(32'h1), .in1(multiplexer_7_out), .out(multiplexer_3_out), .sel(start));
  Multiplexer #(.width(32), .enable("false")) multiplexer_4 (
    .in0(32'h1), .in1(multiplexer_8_out), .out(multiplexer_4_out), .sel(start));
  Register #(.width(32)) register_1 (.D(multiplexer_1_out), .Q(register_1_q), .clk(clk), .clr(clr));  // open: en
  Register #(.width(32)) register_2 (.D(multiplexer_2_out), .Q(out_5), .clk(clk), .clr(clr));  // open: en
  Register #(.width(32)) register_3 (.D(multiplexer_3_out), .Q(register_3_q), .clk(clk), .clr(clr));  // open: en
  Register #(.width(32)) register_4 (.D(multiplexer_4_out), .Q(register_4_q), .clk(clk), .clr(clr));  // open: en
  sqrX_A sqrx_a_1 (
    .a(register_1_q), .b(out_5), .c(register_3_q), .d(register_4_q), .ab_bd(sqrx_a_1_ab_bd),
    .a2_bc_ab_bd(sqrx_a_1_a2_bc_ab_bd), .bc_d2(sqrx_a_1_bc_d2), .ac_cd_bc_d2(sqrx_a_1_ac_cd_bc_d2));
  sqrX sqrx_1 (
    .a(register_1_q), .b(out_5), .c(register_3_q), .d(register_4_q), .a2_bc(sqrx_1_a2_bc),
    .ab_bd(sqrx_1_ab_bd), .ac_cd(sqrx_1_ac_cd), .bc_d2(sqrx_1_bc_d2));
  Multiplexer #(.width(32), .enable("false")) multiplexer_5 (
    .in0(sqrx_1_a2_bc), .in1(sqrx_a_1_ab_bd), .out(multiplexer_5_out), .sel(n_i_1));
  Multiplexer #(.width(32), .enable("false")) multiplexer_6 (
    .in0(sqrx_1_ab_bd), .in1(sqrx_a_1_a2_bc_ab_bd), .out(multiplexer_6_out), .sel(n_i_1));
  Multiplexer #(.width(32), .enable("false")) multiplexer_7 (
    .in0(sqrx_1_ac_cd), .in1(sqrx_a_1_bc_d2), .out(multiplexer_7_out), .sel(n_i_1));
  Multiplexer #(.width(32), .enable("false")) multiplexer_8 (
    .in0(sqrx_1_bc_d2), .in1(sqrx_a_1_ac_cd_bc_d2), .out(multiplexer_8_out), .sel(n_i_1));
endmodule
